// Logisim project FINAL_CPU.circ as structural Verilog
module Add_2 (
  input  A,
  input  B,
  input  Carry_in,
  output Sum,
  output Carry_out
);

  wire and_1_out, and_2_out, xor_1_out;

  // Probe on A
  // Probe on B
  // Probe on Carry_in
  xor xor_1 (xor_1_out, A, B);
  xor xor_2 (Sum, xor_1_out, Carry_in);
  and and_1 (and_1_out, Carry_in, xor_1_out);
  and and_2 (and_2_out, B, A);
  // Probe on Sum
  // Probe on Carry_out
  or or_1 (Carry_out, and_1_out, and_2_out);
endmodule

module Add_4 (
  input  Carry_in,
  input  [3:0] A,
  input  [3:0] B,
  output [3:0] Sum,
  output Carry_out
);

  wire add_2_1_carry_out, add_2_3_carry_out, add_2_4_carry_out;

  // Probe on A
  // Probe on B
  Add_2 add_2_1 (.A(A[0]), .B(B[0]), .Carry_in(Carry_in), .Sum(Sum[0]), .Carry_out(add_2_1_carry_out));
  Add_2 add_2_2 (.A(A[3]), .B(B[3]), .Carry_in(add_2_4_carry_out), .Sum(Sum[3]), .Carry_out(Carry_out));
  LED led_1 (.in(Carry_out));
  Add_2 add_2_3 (.A(A[1]), .B(B[1]), .Carry_in(add_2_1_carry_out), .Sum(Sum[1]), .Carry_out(add_2_3_carry_out));
  Add_2 add_2_4 (.A(A[2]), .B(B[2]), .Carry_in(add_2_3_carry_out), .Sum(Sum[2]), .Carry_out(add_2_4_carry_out));
  // Probe on Sum
endmodule

module Add_8 (
  input  [7:0] A,
  input  Carry_in,
  input  [7:0] B,
  output [7:0] Sum,
  output Carry_out
);

  wire add_4_1_carry_out;

  // Probe on A
  // Probe on B
  Add_4 add_4_1 (.Carry_in(Carry_in), .A(A[3:0]), .B(B[3:0]), .Sum(Sum[3:0]), .Carry_out(add_4_1_carry_out));
  Add_4 add_4_2 (.Carry_in(add_4_1_carry_out), .A(A[7:4]), .B(B[7:4]), .Sum(Sum[7:4]), .Carry_out(Carry_out));
  // Probe on Sum
  LED led_1 (.in(Carry_out));
endmodule

module Add_16 (
  input  [15:0] A,
  input  Carry_in,
  input  [15:0] B,
  output [15:0] Sum,
  output Carry_out
);

  wire add_8_1_carry_out;

  // Probe on A
  // Probe on B
  Add_8 add_8_1 (.A(A[7:0]), .Carry_in(Carry_in), .B(B[7:0]), .Sum(Sum[7:0]), .Carry_out(add_8_1_carry_out));
  Add_8 add_8_2 (.A(A[15:8]), .Carry_in(add_8_1_carry_out), .B(B[15:8]), .Sum(Sum[15:8]), .Carry_out(Carry_out));
  LED led_1 (.in(Carry_out));
  // Probe on Sum
endmodule

module AddSub_16 (
  input  [15:0] A,
  input  Carry_in,
  input  [15:0] B,
  input  [7:0] Sub,
  output [15:0] Sum,
  output Carry_out
);

  wire add_8_1_carry_out;
  wire [7:0] xor_1_out, xor_2_out;

  // Probe on A
  // Probe on B
  assign xor_1_out = Sub ^ B[7:0];  // XOR_Gate xor_1, 8 bits wide
  assign xor_2_out = B[15:8] ^ Sub;  // XOR_Gate xor_2, 8 bits wide
  Add_8 add_8_1 (.A(A[7:0]), .Carry_in(Carry_in), .B(xor_1_out), .Sum(Sum[7:0]), .Carry_out(add_8_1_carry_out));
  Add_8 add_8_2 (.A(A[15:8]), .Carry_in(add_8_1_carry_out), .B(xor_2_out), .Sum(Sum[15:8]), .Carry_out(Carry_out));
  LED led_1 (.in(Carry_out));
  // Probe on Sum
endmodule

module Mult_4 (
  input  [3:0] B,
  input  [3:0] A,
  output [7:0] Product
);

  wire [3:0] add_4_2_carry_out, add_4_3_carry_out, and_4_out, and_8_out, and_12_out, and_15_out;

  // Probe on A
  and and_1 (and_4_out[3], A[3], B[3]);
  and and_2 (and_4_out[2], A[3], B[2]);
  and and_3 (and_4_out[1], A[3], B[1]);
  and and_4 (and_4_out[0], A[3], B[0]);
  and and_5 (and_8_out[3], A[2], B[3]);
  and and_6 (and_8_out[2], A[2], B[2]);
  and and_7 (and_8_out[1], A[2], B[1]);
  and and_8 (and_8_out[0], A[2], B[0]);
  and and_9 (and_12_out[3], A[1], B[3]);
  and and_10 (and_12_out[2], A[1], B[2]);
  Add_4 add_4_1 (.A(add_4_3_carry_out), .B(and_4_out), .Sum(Product[6:3]), .Carry_out(Product[7]));  // open: Carry_in
  and and_11 (and_12_out[1], A[1], B[1]);
  and and_12 (and_12_out[0], A[1], B[0]);
  Add_4 add_4_2 (
    .A(and_15_out), .B(and_12_out), .Sum({add_4_2_carry_out[2:0], Product[1]}),
    .Carry_out(add_4_2_carry_out[3]));  // open: Carry_in
  Add_4 add_4_3 (
    .A(add_4_2_carry_out), .B(and_8_out), .Sum({add_4_3_carry_out[2:0], Product[2]}),
    .Carry_out(add_4_3_carry_out[3]));  // open: Carry_in
  // Probe on Product
  and and_13 (and_15_out[2], A[0], B[3]);
  and and_14 (and_15_out[1], A[0], B[2]);
  and and_15 (and_15_out[0], A[0], B[1]);
  // Probe on B
  and and_16 (Product[0], A[0], B[0]);
endmodule

module Instruction_splitter (
  input  [15:0] Instruction,
  input  Write_Enable,
  input  Clock,
  output [4:0] Add_B,
  output [4:0] Add_A,
  output [4:0] Opcode,
  output Flag
);

  Register #(.width(16)) register_1 (
    .D(Instruction), .en(Write_Enable), .clk(Clock), .Q({Flag, Opcode, Add_A, Add_B}));  // open: clr
endmodule

module Mult_16 (
  input  [7:0] A,
  input  [7:0] B,
  output [15:0] Product_16bit,
  output C_out
);

  wire [3:0] undriven_2, undriven_3;
  wire [7:0] mult_4_1_product, mult_4_2_product, mult_4_3_product, mult_4_4_product, undriven, undriven_5;
  wire [15:0] add_16_1_sum, add_16_2_sum, undriven_4;

  // Probe on A
  // Probe on B
  // Probe on A[3:0]
  // Probe on A[7:4]
  // Probe on B[3:0]
  // Probe on B[7:4]
  // Probe on mult_4_1_product
  Mult_4 mult_4_1 (.B(B[3:0]), .A(A[3:0]), .Product(mult_4_1_product));
  // Probe on mult_4_2_product
  Mult_4 mult_4_2 (.B(B[7:4]), .A(A[3:0]), .Product(mult_4_2_product));
  // Probe on mult_4_3_product
  Mult_4 mult_4_3 (.B(B[3:0]), .A(A[7:4]), .Product(mult_4_3_product));
  // Probe on mult_4_4_product
  Mult_4 mult_4_4 (.B(B[7:4]), .A(A[7:4]), .Product(mult_4_4_product));
  Add_16 add_16_1 (
    .A({undriven, mult_4_1_product}), .B({undriven_3, mult_4_2_product, undriven_2}), .Sum(add_16_1_sum));  // open: Carry_in, Carry_out
  Add_16 add_16_2 (
    .A({undriven_4[15:12], mult_4_3_product, undriven_4[3:0]}), .B({mult_4_4_product, undriven_5}),
    .Sum(add_16_2_sum));  // open: Carry_in, Carry_out
  // Probe on add_16_1_sum
  // Probe on add_16_2_sum
  // Probe on Product_16bit
  Add_16 add_16_3 (.A(add_16_1_sum), .B(add_16_2_sum), .Sum(Product_16bit), .Carry_out(C_out));  // open: Carry_in
  LED led_1 (.in(C_out));
endmodule

module Comaparator_1bit (
  input  A,
  input  B,
  output L_out,
  output E_out,
  output G_out
);

  wire not_1_out, not_2_out;

  not not_1 (not_1_out, A);
  not not_2 (not_2_out, B);
  and and_1 (L_out, not_1_out, B);
  and and_2 (G_out, A, not_2_out);
  nor nor_1 (E_out, L_out, G_out);
endmodule

module ALU (
  input  [15:0] A,
  input  [15:0] B,
  input  Flag,
  input  [4:0] Opcode,
  output [15:0] RESULT,
  output [15:0] OVERFLOW_OUT
);

  wire addsub_16_1_carry_out, comparator_16bit_1_e_out, comparator_16bit_1_g_out, comparator_16bit_1_l_out,
       final_final_pakka_wala_decoder_1_add_sub, final_final_pakka_wala_decoder_1_compare,
       final_final_pakka_wala_decoder_1_logical_and, final_final_pakka_wala_decoder_1_logical_not,
       final_final_pakka_wala_decoder_1_logical_xor, final_final_pakka_wala_decoder_1_mult, not_2_out;
  wire [3:0] controlled_buffer_1_out, controlled_buffer_7_out;
  wire [7:0] bit_extender_1_out;
  wire [15:0] addsub_16_1_sum, and_1_out, bit_extender_2_out, mult_16_1_product_16bit, not_1_out, xor_1_out;

  assign bit_extender_1_out = {{7{Flag}}, Flag};  // Bit_Extender bit_extender_1
  comparator_16bit comparator_16bit_1 (
    .A(A), .B(B), .L_out(comparator_16bit_1_l_out), .E_out(comparator_16bit_1_e_out),
    .G_out(comparator_16bit_1_g_out));
  assign and_1_out = A & B;  // AND_Gate and_1, 16 bits wide
  assign not_1_out = ~A;  // NOT_Gate not_1, 16 bits wide
  assign xor_1_out = A ^ B;  // XOR_Gate xor_1, 16 bits wide
  assign controlled_buffer_1_out = comparator_16bit_1_l_out ? 4'b0001 : 4'bz;  // Controlled_Buffer controlled_buffer_1
  assign controlled_buffer_1_out = comparator_16bit_1_e_out ? 4'b0010 : 4'bz;  // Controlled_Buffer controlled_buffer_2
  assign controlled_buffer_1_out = comparator_16bit_1_g_out ? 4'b0100 : 4'bz;  // Controlled_Buffer controlled_buffer_3
  AddSub_16 addsub_16_1 (
    .A(A), .B(B), .Sub(bit_extender_1_out), .Sum(addsub_16_1_sum), .Carry_out(addsub_16_1_carry_out));  // open: Carry_in
  Mult_16 mult_16_1 (.A(A[7:0]), .B(B[7:0]), .Product_16bit(mult_16_1_product_16bit));  // open: C_out
  Final_Final_Pakka_Wala_Decoder final_final_pakka_wala_decoder_1 (
    .A(Flag), .B(Opcode[3]), .C(Opcode[2]), .D(Opcode[1]), .E(Opcode[0]),
    .ADD_SUB(final_final_pakka_wala_decoder_1_add_sub), .MULT(final_final_pakka_wala_decoder_1_mult),
    .COMPARE(final_final_pakka_wala_decoder_1_compare),
    .LOGICAL_AND(final_final_pakka_wala_decoder_1_logical_and),
    .LOGICAL_XOR(final_final_pakka_wala_decoder_1_logical_xor),
    .LOGICAL_NOT(final_final_pakka_wala_decoder_1_logical_not));
  assign bit_extender_2_out = {{15{1'b0}}, addsub_16_1_carry_out};  // Bit_Extender bit_extender_2
  assign RESULT = final_final_pakka_wala_decoder_1_add_sub ? addsub_16_1_sum : 16'bz;  // Controlled_Buffer controlled_buffer_4
  assign OVERFLOW_OUT = final_final_pakka_wala_decoder_1_add_sub ? bit_extender_2_out : 16'bz;  // Controlled_Buffer controlled_buffer_5
  assign RESULT = final_final_pakka_wala_decoder_1_mult ? mult_16_1_product_16bit : 16'bz;  // Controlled_Buffer controlled_buffer_6
  not not_2 (not_2_out, final_final_pakka_wala_decoder_1_add_sub);
  assign controlled_buffer_7_out = final_final_pakka_wala_decoder_1_compare ? controlled_buffer_1_out : 4'bz;  // Controlled_Buffer controlled_buffer_7
  assign OVERFLOW_OUT = not_2_out ? {16{1'b0}} : 16'bz;  // Controlled_Buffer controlled_buffer_8
  assign RESULT = final_final_pakka_wala_decoder_1_logical_and ? and_1_out : 16'bz;  // Controlled_Buffer controlled_buffer_9
  assign RESULT = final_final_pakka_wala_decoder_1_logical_xor ? xor_1_out : 16'bz;  // Controlled_Buffer controlled_buffer_10
  assign RESULT = final_final_pakka_wala_decoder_1_logical_not ? not_1_out : 16'bz;  // Controlled_Buffer controlled_buffer_11
  assign RESULT = {{12{controlled_buffer_7_out[3]}}, controlled_buffer_7_out};  // Bit_Extender bit_extender_3

  // Notes on the sheet:
  //   MSB(RIGHT SIDE)
  //   LSB (LEFT SIDE)
endmodule

module comparator_2bit (
  input  [1:0] A,
  input  [1:0] B,
  output L_out,
  output E_out,
  output G_out
);

  wire and_1_out, and_2_out, and_3_out, and_4_out, and_6_out, and_7_out, comaparator_1bit_1_e_out,
       comaparator_1bit_1_g_out, comaparator_1bit_1_l_out, comaparator_1bit_2_e_out,
       comaparator_1bit_2_g_out, comaparator_1bit_2_l_out, not_1_out, not_2_out, not_3_out, not_4_out;

  Comaparator_1bit comaparator_1bit_1 (
    .A(A[0]), .B(B[0]), .L_out(comaparator_1bit_1_l_out), .E_out(comaparator_1bit_1_e_out),
    .G_out(comaparator_1bit_1_g_out));
  Comaparator_1bit comaparator_1bit_2 (
    .A(A[1]), .B(B[1]), .L_out(comaparator_1bit_2_l_out), .E_out(comaparator_1bit_2_e_out),
    .G_out(comaparator_1bit_2_g_out));
  not not_1 (not_1_out, comaparator_1bit_1_l_out);
  not not_2 (not_2_out, comaparator_1bit_1_g_out);
  not not_3 (not_3_out, comaparator_1bit_2_l_out);
  not not_4 (not_4_out, comaparator_1bit_2_g_out);
  and and_1 (and_1_out, comaparator_1bit_1_g_out, not_1_out);
  and and_2 (and_2_out, not_2_out, comaparator_1bit_1_l_out);
  and and_3 (and_3_out, comaparator_1bit_2_g_out, not_3_out);
  and and_4 (and_4_out, not_4_out, comaparator_1bit_2_l_out);
  and and_5 (G_out, and_1_out, comaparator_1bit_2_e_out);
  and and_6 (and_6_out, comaparator_1bit_1_e_out, comaparator_1bit_2_e_out);
  and and_7 (and_7_out, and_2_out, comaparator_1bit_2_e_out);
  or or_1 (L_out, and_7_out, and_4_out);
  or or_2 (E_out, and_6_out, and_3_out);
endmodule

module Final_Final_Pakka_Wala_Decoder (
  input  A,
  input  B,
  input  C,
  input  D,
  input  E,
  output ADD_SUB,
  output MULT,
  output COMPARE,
  output LOGICAL_AND,
  output LOGICAL_XOR,
  output LOGICAL_NOT
);

  wire not_1_out, not_2_out, not_3_out, not_4_out, not_5_out;

  not not_1 (not_1_out, A);
  not not_2 (not_2_out, B);
  not not_3 (not_3_out, C);
  not not_4 (not_4_out, D);
  not not_5 (not_5_out, E);
  and and_1 (ADD_SUB, not_1_out, not_2_out, not_3_out, not_4_out, E);
  and and_2 (MULT, not_2_out, D, E);
  and and_3 (COMPARE, B, D, not_5_out);
  and and_4 (LOGICAL_AND, B, D, E);
  and and_5 (LOGICAL_XOR, B, not_4_out, not_5_out);
  and and_6 (LOGICAL_NOT, B, not_4_out, E);
endmodule

module comparator_4bit (
  input  [3:0] A,
  input  [3:0] B,
  output L_out,
  output E_out,
  output G_out
);

  wire and_1_out, and_2_out, and_3_out, and_4_out, and_6_out, and_7_out, comparator_2bit_1_e_out,
       comparator_2bit_1_g_out, comparator_2bit_1_l_out, comparator_2bit_2_e_out, comparator_2bit_2_g_out,
       comparator_2bit_2_l_out, not_1_out, not_2_out, not_3_out, not_4_out;

  comparator_2bit comparator_2bit_1 (
    .A(A[1:0]), .B(B[1:0]), .L_out(comparator_2bit_1_l_out), .E_out(comparator_2bit_1_e_out),
    .G_out(comparator_2bit_1_g_out));
  comparator_2bit comparator_2bit_2 (
    .A(A[3:2]), .B(B[3:2]), .L_out(comparator_2bit_2_l_out), .E_out(comparator_2bit_2_e_out),
    .G_out(comparator_2bit_2_g_out));
  not not_1 (not_1_out, comparator_2bit_1_l_out);
  not not_2 (not_2_out, comparator_2bit_1_g_out);
  not not_3 (not_3_out, comparator_2bit_2_l_out);
  not not_4 (not_4_out, comparator_2bit_2_g_out);
  and and_1 (and_1_out, comparator_2bit_1_g_out, not_1_out);
  and and_2 (and_2_out, comparator_2bit_2_g_out, not_3_out);
  and and_3 (and_3_out, not_4_out, comparator_2bit_2_l_out);
  and and_4 (and_4_out, not_2_out, comparator_2bit_1_l_out);
  and and_5 (G_out, and_1_out, comparator_2bit_2_e_out);
  and and_6 (and_6_out, comparator_2bit_1_e_out, comparator_2bit_2_e_out);
  and and_7 (and_7_out, and_4_out, comparator_2bit_2_e_out);
  or or_1 (E_out, and_6_out, and_2_out);
  or or_2 (L_out, and_7_out, and_3_out);
endmodule

module comparator_8bit (
  input  [7:0] A,
  input  [7:0] B,
  output L_out,
  output E_out,
  output G_out
);

  wire and_1_out, and_2_out, and_3_out, and_4_out, and_6_out, and_7_out, comparator_4bit_1_e_out,
       comparator_4bit_1_g_out, comparator_4bit_1_l_out, comparator_4bit_2_e_out, comparator_4bit_2_g_out,
       comparator_4bit_2_l_out, not_1_out, not_2_out, not_3_out, not_4_out;

  comparator_4bit comparator_4bit_1 (
    .A(A[3:0]), .B(B[3:0]), .L_out(comparator_4bit_1_l_out), .E_out(comparator_4bit_1_e_out),
    .G_out(comparator_4bit_1_g_out));
  comparator_4bit comparator_4bit_2 (
    .A(A[7:4]), .B(B[7:4]), .L_out(comparator_4bit_2_l_out), .E_out(comparator_4bit_2_e_out),
    .G_out(comparator_4bit_2_g_out));
  not not_1 (not_1_out, comparator_4bit_1_l_out);
  not not_2 (not_2_out, comparator_4bit_1_g_out);
  not not_3 (not_3_out, comparator_4bit_2_l_out);
  not not_4 (not_4_out, comparator_4bit_2_g_out);
  and and_1 (and_1_out, comparator_4bit_1_g_out, not_1_out);
  and and_2 (and_2_out, comparator_4bit_2_g_out, not_3_out);
  and and_3 (and_3_out, not_4_out, comparator_4bit_2_l_out);
  and and_4 (and_4_out, not_2_out, comparator_4bit_1_l_out);
  and and_5 (G_out, and_1_out, comparator_4bit_2_e_out);
  and and_6 (and_6_out, comparator_4bit_1_e_out, comparator_4bit_2_e_out);
  and and_7 (and_7_out, and_4_out, comparator_4bit_2_e_out);
  or or_1 (E_out, and_6_out, and_2_out);
  or or_2 (L_out, and_7_out, and_3_out);
endmodule

module comparator_16bit (
  input  [15:0] A,
  input  [15:0] B,
  output L_out,
  output E_out,
  output G_out
);

  wire and_1_out, and_2_out, and_3_out, and_4_out, and_6_out, and_7_out, comparator_8bit_1_e_out,
       comparator_8bit_1_g_out, comparator_8bit_1_l_out, comparator_8bit_2_e_out, comparator_8bit_2_g_out,
       comparator_8bit_2_l_out, not_1_out, not_2_out, not_3_out, not_4_out;

  comparator_8bit comparator_8bit_1 (
    .A(A[7:0]), .B(B[7:0]), .L_out(comparator_8bit_1_l_out), .E_out(comparator_8bit_1_e_out),
    .G_out(comparator_8bit_1_g_out));
  comparator_8bit comparator_8bit_2 (
    .A(A[15:8]), .B(B[15:8]), .L_out(comparator_8bit_2_l_out), .E_out(comparator_8bit_2_e_out),
    .G_out(comparator_8bit_2_g_out));
  not not_1 (not_1_out, comparator_8bit_1_l_out);
  not not_2 (not_2_out, comparator_8bit_1_g_out);
  not not_3 (not_3_out, comparator_8bit_2_l_out);
  not not_4 (not_4_out, comparator_8bit_2_g_out);
  and and_1 (and_1_out, comparator_8bit_1_g_out, not_1_out);
  and and_2 (and_2_out, not_2_out, comparator_8bit_1_l_out);
  and and_3 (and_3_out, comparator_8bit_2_g_out, not_3_out);
  and and_4 (and_4_out, not_4_out, comparator_8bit_2_l_out);
  and and_5 (G_out, and_1_out, comparator_8bit_2_e_out);
  and and_6 (and_6_out, comparator_8bit_1_e_out, comparator_8bit_2_e_out);
  and and_7 (and_7_out, and_2_out, comparator_8bit_2_e_out);
  or or_1 (L_out, and_7_out, and_4_out);
  or or_2 (E_out, and_6_out, and_3_out);
endmodule

module Final_Final_Final_Wala_Circuit_Hopefully_useless (
  input  OPCODE_INIT_CB,
  input  OPCODE_REG_WE,
  input  COUNTER_RESET,
  input  COUNTER_INC_BY1,
  input  COUNTER_INC_ON,
  input  MEMB_WE,
  input  SYSMEM_WE,
  input  INSTMEM_WE,
  input  MEMA_WE,
  input  MBRZ_OE,
  input  MBRA_OE,
  input  MBRB_OE,
  input  MBRZ_WE,
  input  MBRA_WE,
  input  MBRB_WE,
  input  REG8_WE,
  input  REG7_WE,
  input  REG6_WE,
  input  REG5_WE,
  input  REG4_WE,
  input  REG3_WE,
  input  REG2_WE,
  input  REG1_WE,
  input  INST_SPLITTER_WE,
  input  MARB_WE,
  input  MARA_WE,
  input  MARZ_WE,
  input  INSTMEM_OE,
  input  SYSMEM_OE,
  input  MEMB_OE,
  input  MEMA_OE,
  input  OUTPUT_REG_WE,
  input  REG_1_OE,
  input  REG_3_OE,
  input  REG_5_OE,
  input  REG_7_OE,
  input  REG_2_OE,
  input  REG_4_OE,
  input  REG_6_OE,
  input  REG_8_OE
);

  wire Clk_out, instruction_splitter_1_flag, PROGRAM_COUNTER_carry;
  wire [3:0] counter_1_q;
  wire [4:0] controlled_buffer_1_out, instruction_splitter_1_add_a, instruction_splitter_1_add_b, MAR_A_q,
       MAR_B_q, MAR_Zero_q, PROGRAM_COUNTER_q, register_2_q;
  wire [15:0] alu_1_result, controlled_buffer_2_out, controlled_buffer_3_out, controlled_buffer_10_out,
       controlled_buffer_11_out, controlled_buffer_12_out, inst_mem_dout, MBR_A_q, MBR_B_q, MBR_Z_q,
       RAM_A_dout, RAM_B_dout, Reg_1_q, Reg_2_q, Reg_3_q, Reg_4_q, Reg_5_q, Reg_6_q, Reg_7_q, Reg_8_q,
       register_1_q;
  wire [39:0] ROM_PCU_data;

  ALU alu_1 (
    .A(controlled_buffer_2_out), .B(controlled_buffer_3_out), .Flag(instruction_splitter_1_flag),
    .Opcode(controlled_buffer_1_out), .RESULT(alu_1_result));  // open: OVERFLOW_OUT
  // Probe on ROM_PCU_data[37]
  // Probe on ROM_PCU_data[35]
  Register #(.width(16)) register_1 (
    .D(alu_1_result), .en(ROM_PCU_data[8]), .clk(Clk_out), .Q(register_1_q));  // open: clr
  Counter #(.max('h1f), .width(5)) PROGRAM_COUNTER (
    .clr(ROM_PCU_data[37]), .up(ROM_PCU_data[35]), .count(ROM_PCU_data[36]), .clk(Clk_out),
    .carry(PROGRAM_COUNTER_carry), .Q(PROGRAM_COUNTER_q));  // open: load, D
  Register #(.width(5)) register_2 (
    .D(controlled_buffer_1_out), .en(ROM_PCU_data[38]), .clk(Clk_out), .Q(register_2_q));  // open: clr
  // Probe on PROGRAM_COUNTER_carry
  assign controlled_buffer_1_out = ROM_PCU_data[39] ? {5{1'b0}} : 5'bz;  // Controlled_Buffer controlled_buffer_1
  Instruction_splitter instruction_splitter_1 (
    .Instruction(controlled_buffer_10_out), .Write_Enable(ROM_PCU_data[16]), .Clock(Clk_out),
    .Add_B(instruction_splitter_1_add_b), .Add_A(instruction_splitter_1_add_a),
    .Opcode(controlled_buffer_1_out), .Flag(instruction_splitter_1_flag));
  Register #(.width(5)) MAR_Zero (
    .D(PROGRAM_COUNTER_q), .en(ROM_PCU_data[13]), .clk(Clk_out), .Q(MAR_Zero_q));  // open: clr
  Register #(.width(16)) Reg_1 (
    .D(controlled_buffer_11_out), .en(ROM_PCU_data[17]), .clk(Clk_out), .Q(Reg_1_q));  // open: clr
  Register #(.width(16)) Reg_3 (
    .D(controlled_buffer_11_out), .en(ROM_PCU_data[19]), .clk(Clk_out), .Q(Reg_3_q));  // open: clr
  Register #(.width(16)) Reg_5 (
    .D(controlled_buffer_12_out), .en(ROM_PCU_data[21]), .clk(Clk_out), .Q(Reg_5_q));  // open: clr
  Register #(.width(16)) Reg_7 (
    .D(controlled_buffer_12_out), .en(ROM_PCU_data[23]), .clk(Clk_out), .Q(Reg_7_q));  // open: clr
  assign controlled_buffer_2_out = ROM_PCU_data[6] ? Reg_3_q : 16'bz;  // Controlled_Buffer controlled_buffer_2
  assign controlled_buffer_3_out = ROM_PCU_data[5] ? Reg_5_q : 16'bz;  // Controlled_Buffer controlled_buffer_3
  Register #(.width(5)) MAR_A (
    .D(instruction_splitter_1_add_a), .en(ROM_PCU_data[14]), .clk(Clk_out), .Q(MAR_A_q));  // open: clr
  assign controlled_buffer_2_out = ROM_PCU_data[7] ? Reg_1_q : 16'bz;  // Controlled_Buffer controlled_buffer_4
  Register #(.width(16)) Reg_2 (
    .D(controlled_buffer_11_out), .en(ROM_PCU_data[18]), .clk(Clk_out), .Q(Reg_2_q));  // open: clr
  Register #(.width(16)) Reg_4 (
    .D(controlled_buffer_11_out), .en(ROM_PCU_data[20]), .clk(Clk_out), .Q(Reg_4_q));  // open: clr
  Register #(.width(16)) Reg_6 (
    .D(controlled_buffer_12_out), .en(ROM_PCU_data[22]), .clk(Clk_out), .Q(Reg_6_q));  // open: clr
  assign controlled_buffer_3_out = ROM_PCU_data[4] ? Reg_7_q : 16'bz;  // Controlled_Buffer controlled_buffer_5
  Register #(.width(16)) Reg_8 (
    .D(controlled_buffer_12_out), .en(ROM_PCU_data[24]), .clk(Clk_out), .Q(Reg_8_q));  // open: clr
  assign controlled_buffer_2_out = ROM_PCU_data[3] ? Reg_2_q : 16'bz;  // Controlled_Buffer controlled_buffer_6
  assign controlled_buffer_2_out = ROM_PCU_data[2] ? Reg_4_q : 16'bz;  // Controlled_Buffer controlled_buffer_7
  assign controlled_buffer_3_out = ROM_PCU_data[1] ? Reg_6_q : 16'bz;  // Controlled_Buffer controlled_buffer_8
  assign controlled_buffer_3_out = ROM_PCU_data[0] ? Reg_8_q : 16'bz;  // Controlled_Buffer controlled_buffer_9
  Register #(.width(5)) MAR_B (
    .D(instruction_splitter_1_add_b), .en(ROM_PCU_data[15]), .clk(Clk_out), .Q(MAR_B_q));  // open: clr
  Clock Clk (.out(Clk_out));
  Register #(.width(16)) MBR_Z (.D(inst_mem_dout), .en(ROM_PCU_data[27]), .clk(Clk_out), .Q(MBR_Z_q));  // open: clr
  Register #(.width(16)) MBR_A (.D(RAM_A_dout), .en(ROM_PCU_data[26]), .clk(Clk_out), .Q(MBR_A_q));  // open: clr
  Register #(.width(16)) MBR_B (.D(RAM_B_dout), .en(ROM_PCU_data[25]), .clk(Clk_out), .Q(MBR_B_q));  // open: clr
  assign controlled_buffer_10_out = ROM_PCU_data[30] ? MBR_Z_q : 16'bz;  // Controlled_Buffer controlled_buffer_10
  assign controlled_buffer_11_out = ROM_PCU_data[29] ? MBR_A_q : 16'bz;  // Controlled_Buffer controlled_buffer_11
  assign controlled_buffer_12_out = ROM_PCU_data[28] ? MBR_B_q : 16'bz;  // Controlled_Buffer controlled_buffer_12
  RAM #(.addrWidth(5), .dataWidth(16)) inst_mem (
    .addr(MAR_Zero_q), .we(ROM_PCU_data[32]), .oe(ROM_PCU_data[12]), .clk(Clk_out),
    .din(controlled_buffer_10_out), .dout(inst_mem_dout));
  RAM #(.addrWidth(5), .dataWidth(16)) RAM_A (
    .addr(MAR_A_q), .we(ROM_PCU_data[31]), .oe(ROM_PCU_data[9]), .clk(Clk_out),
    .din(controlled_buffer_11_out), .dout(RAM_A_dout));
  RAM #(.addrWidth(5), .dataWidth(16)) SYS_MEM (
    .addr(MAR_A_q), .we(ROM_PCU_data[33]), .oe(ROM_PCU_data[11]), .clk(Clk_out), .din(register_1_q),
    .dout(inst_mem_dout));
  RAM #(.addrWidth(5), .dataWidth(16)) RAM_B (
    .addr(MAR_B_q), .we(ROM_PCU_data[34]), .oe(ROM_PCU_data[10]), .clk(Clk_out),
    .din(controlled_buffer_12_out), .dout(RAM_B_dout));
  ROM #(.dataWidth(40)) ROM_PCU (.addr({register_2_q[3:0], counter_1_q}), .data(ROM_PCU_data));
  Counter #(.max('ha), .width(4)) counter_1 (
    .up(1'b1), .count(1'b1), .clk(Clk_out), .Q(counter_1_q));  // open: clr, load, D, carry

  // Notes on the sheet:
  //   contents of ROM_PCU (hex, n*v repeats v):
  //   c800002000 1800001000 808000000 840010000 80000c000 4800000000 800000600 806000000 830220000 8000001
  //   a000000 5*0 48000020 18000010 8080000 8400100 80000c0 48000000 8000006 8060000 8302200 8000001
  //   a000000 5*0 48000020 18000010 8080000 8400100 80000c0 48000000 8000006 8060000 8302200 8000001
  //   a000000 5*0 48000020 18000010 8080000 8400100 80000c0 48000000 8000006 8060000 8302200 8000001
  //   a000000 5*0 48000020 18000010 8080000 8400100 80000c0 48000000 8000006 8060000 8302200 8000001
  //   a000000 5*0 48000020 18000010 8080000 8400100 80000c0 48000000 8000006 8060000 8302200 8000001
  //   a000000 5*0 48000020 18000010 8080000 8400100 80000c0 48000000 8000006 8060000 8302200 8000001
  //   a000000 5*0 48000020 18000010 8080000 8400100 80000c0 48000000 8000006 8060000 8302200 8000001
  //   a000000
endmodule

module MAT_MULT (
  input  [15:0] REG_1,
  input  [15:0] REG_5,
  input  [15:0] REG_2,
  input  [15:0] REG_7,
  input  [15:0] REG_6,
  input  [15:0] REG_8,
  input  [15:0] REG_3,
  input  [15:0] REG_4,
  output [15:0] PROD1_TOPLEFT,
  output [15:0] PROD2_TOPRIGHT,
  output [15:0] PROD3_BOTTOMLEFT,
  output [15:0] PROD4_BOTTOMRIGHT
);

  wire [7:0] bit_extender_1_out, bit_extender_2_out, bit_extender_3_out, bit_extender_4_out,
       bit_extender_5_out, bit_extender_6_out, bit_extender_7_out, bit_extender_8_out;
  wire [15:0] mult_16_1_product_16bit, mult_16_2_product_16bit, mult_16_3_product_16bit,
       mult_16_4_product_16bit, mult_16_5_product_16bit, mult_16_6_product_16bit, mult_16_7_product_16bit,
       mult_16_8_product_16bit;

  Bit_Extender #(.in_width(16), .out_width(8)) bit_extender_1 (.in(REG_6), .out(bit_extender_1_out));
  Bit_Extender #(.in_width(16), .out_width(8)) bit_extender_2 (.in(REG_1), .out(bit_extender_2_out));
  Bit_Extender #(.in_width(16), .out_width(8)) bit_extender_3 (.in(REG_5), .out(bit_extender_3_out));
  Bit_Extender #(.in_width(16), .out_width(8)) bit_extender_4 (.in(REG_2), .out(bit_extender_4_out));
  Bit_Extender #(.in_width(16), .out_width(8)) bit_extender_5 (.in(REG_7), .out(bit_extender_5_out));
  Bit_Extender #(.in_width(16), .out_width(8)) bit_extender_6 (.in(REG_8), .out(bit_extender_6_out));
  Bit_Extender #(.in_width(16), .out_width(8)) bit_extender_7 (.in(REG_3), .out(bit_extender_7_out));
  Bit_Extender #(.in_width(16), .out_width(8)) bit_extender_8 (.in(REG_4), .out(bit_extender_8_out));
  // Probe on bit_extender_7_out
  // Probe on bit_extender_8_out
  // Probe on bit_extender_5_out
  // Probe on bit_extender_2_out
  // Probe on bit_extender_3_out
  // Probe on bit_extender_4_out
  // Probe on bit_extender_5_out
  // Probe on bit_extender_4_out
  // Probe on bit_extender_6_out
  // Probe on bit_extender_3_out
  // Probe on bit_extender_7_out
  // Probe on bit_extender_1_out
  // Probe on bit_extender_8_out
  // Probe on bit_extender_6_out
  // Probe on bit_extender_2_out
  // Probe on bit_extender_1_out
  Mult_16 mult_16_1 (
    .A(bit_extender_4_out), .B(bit_extender_6_out), .Product_16bit(mult_16_1_product_16bit));  // open: C_out
  Mult_16 mult_16_2 (
    .A(bit_extender_8_out), .B(bit_extender_5_out), .Product_16bit(mult_16_2_product_16bit));  // open: C_out
  Mult_16 mult_16_3 (
    .A(bit_extender_8_out), .B(bit_extender_6_out), .Product_16bit(mult_16_3_product_16bit));  // open: C_out
  Mult_16 mult_16_4 (
    .A(bit_extender_2_out), .B(bit_extender_3_out), .Product_16bit(mult_16_4_product_16bit));  // open: C_out
  Mult_16 mult_16_5 (
    .A(bit_extender_4_out), .B(bit_extender_5_out), .Product_16bit(mult_16_5_product_16bit));  // open: C_out
  Mult_16 mult_16_6 (
    .A(bit_extender_2_out), .B(bit_extender_1_out), .Product_16bit(mult_16_6_product_16bit));  // open: C_out
  Mult_16 mult_16_7 (
    .A(bit_extender_7_out), .B(bit_extender_3_out), .Product_16bit(mult_16_7_product_16bit));  // open: C_out
  Mult_16 mult_16_8 (
    .A(bit_extender_7_out), .B(bit_extender_1_out), .Product_16bit(mult_16_8_product_16bit));  // open: C_out
  // Probe on mult_16_8_product_16bit
  // Probe on mult_16_3_product_16bit
  // Probe on mult_16_4_product_16bit
  // Probe on mult_16_5_product_16bit
  // Probe on mult_16_1_product_16bit
  // Probe on mult_16_2_product_16bit
  // Probe on mult_16_6_product_16bit
  // Probe on mult_16_7_product_16bit
  Add_16 add_16_1 (
    .A(mult_16_4_product_16bit), .B(mult_16_5_product_16bit), .Sum(PROD1_TOPLEFT));  // open: Carry_in, Carry_out
  Add_16 add_16_2 (
    .A(mult_16_6_product_16bit), .B(mult_16_1_product_16bit), .Sum(PROD2_TOPRIGHT));  // open: Carry_in, Carry_out
  Add_16 add_16_3 (
    .A(mult_16_7_product_16bit), .B(mult_16_2_product_16bit), .Sum(PROD3_BOTTOMLEFT));  // open: Carry_in, Carry_out
  Add_16 add_16_4 (
    .A(mult_16_8_product_16bit), .B(mult_16_3_product_16bit), .Sum(PROD4_BOTTOMRIGHT));  // open: Carry_in, Carry_out
  // Probe on PROD4_BOTTOMRIGHT
  // Probe on PROD1_TOPLEFT
  // Probe on PROD2_TOPRIGHT
  // Probe on PROD3_BOTTOMLEFT
endmodule

module REG_SWAP (
  input  [4:0] ADD_A,
  input  [4:0] ADD_B,
  output REG_1_SWAP,
  output REG_2_SWAP,
  output REG_3_SWAP,
  output REG_4_SWAP,
  output REG_5_SWAP,
  output REG_6_SWAP,
  output REG_7_SWAP,
  output REG_8_SWAP
);

  wire and_1_out, and_2_out, and_3_out, and_4_out, and_5_out, and_6_out, and_7_out, and_8_out,
       controlled_buffer_2_out, controlled_buffer_3_out, controlled_buffer_4_out, controlled_buffer_5_out,
       controlled_buffer_8_out, controlled_buffer_9_out, controlled_buffer_10_out, controlled_buffer_11_out,
       not_1_out, not_2_out, not_3_out, not_4_out, not_5_out, not_6_out, not_7_out, not_8_out, not_9_out,
       not_10_out;
  wire [15:0] controlled_buffer_1_out, controlled_buffer_7_out, undriven, undriven_2, undriven_3, undriven_4,
       undriven_5, undriven_6, undriven_7, undriven_8;

  not not_1 (not_1_out, ADD_B[0]);
  not not_2 (not_2_out, ADD_B[1]);
  not not_3 (not_3_out, ADD_B[2]);
  not not_4 (not_4_out, ADD_B[3]);
  not not_5 (not_5_out, ADD_B[4]);
  not not_6 (not_6_out, ADD_A[0]);
  not not_7 (not_7_out, ADD_A[1]);
  not not_8 (not_8_out, ADD_A[2]);
  not not_9 (not_9_out, ADD_A[3]);
  not not_10 (not_10_out, ADD_A[4]);
  and and_1 (and_1_out, ADD_A[0], not_7_out, not_8_out, not_9_out, not_10_out);
  and and_2 (and_2_out, not_6_out, ADD_A[1], not_8_out, not_9_out, not_10_out);
  and and_3 (and_3_out, ADD_A[0], ADD_A[1], not_8_out, not_9_out, not_10_out);
  and and_4 (and_4_out, not_6_out, not_7_out, ADD_A[2], not_9_out, not_10_out);
  and and_5 (and_5_out, ADD_B[0], not_2_out, ADD_B[2], not_4_out, not_5_out);
  and and_6 (and_6_out, not_1_out, ADD_B[1], ADD_B[2], not_4_out, not_5_out);
  and and_7 (and_7_out, ADD_B[0], ADD_B[1], ADD_B[2], not_4_out, not_5_out);
  and and_8 (and_8_out, not_1_out, not_2_out, not_3_out, ADD_B[3], not_5_out);
  assign controlled_buffer_1_out = controlled_buffer_2_out ? undriven_3 : 16'bz;  // Controlled_Buffer controlled_buffer_1
  assign controlled_buffer_2_out = and_1_out ? and_1_out : 1'bz;  // Controlled_Buffer controlled_buffer_2
  assign controlled_buffer_3_out = and_2_out ? and_2_out : 1'bz;  // Controlled_Buffer controlled_buffer_3
  assign controlled_buffer_4_out = and_3_out ? and_3_out : 1'bz;  // Controlled_Buffer controlled_buffer_4
  assign controlled_buffer_5_out = and_4_out ? and_4_out : 1'bz;  // Controlled_Buffer controlled_buffer_5
  assign controlled_buffer_1_out = controlled_buffer_5_out ? undriven_4 : 16'bz;  // Controlled_Buffer controlled_buffer_6
  assign controlled_buffer_7_out = controlled_buffer_8_out ? undriven : 16'bz;  // Controlled_Buffer controlled_buffer_7
  assign controlled_buffer_8_out = and_5_out ? and_5_out : 1'bz;  // Controlled_Buffer controlled_buffer_8
  assign controlled_buffer_9_out = and_6_out ? and_6_out : 1'bz;  // Controlled_Buffer controlled_buffer_9
  assign controlled_buffer_10_out = and_7_out ? and_7_out : 1'bz;  // Controlled_Buffer controlled_buffer_10
  assign controlled_buffer_11_out = and_8_out ? and_8_out : 1'bz;  // Controlled_Buffer controlled_buffer_11
  assign controlled_buffer_7_out = controlled_buffer_11_out ? undriven_2 : 16'bz;  // Controlled_Buffer controlled_buffer_12
  assign controlled_buffer_1_out = controlled_buffer_3_out ? undriven_7 : 16'bz;  // Controlled_Buffer controlled_buffer_13
  assign controlled_buffer_1_out = controlled_buffer_4_out ? undriven_8 : 16'bz;  // Controlled_Buffer controlled_buffer_14
  assign controlled_buffer_7_out = controlled_buffer_9_out ? undriven_5 : 16'bz;  // Controlled_Buffer controlled_buffer_15
  assign controlled_buffer_7_out = controlled_buffer_10_out ? undriven_6 : 16'bz;  // Controlled_Buffer controlled_buffer_16
endmodule

module with_block_load_and_store_useless (
  input  OPCODE_INIT_CB,
  input  OPCODE_REG_WE,
  input  COUNTER_RESET,
  input  COUNTER_INC_BY1,
  input  COUNTER_INC_ON,
  input  MEMB_WE,
  input  SYSMEM_WE,
  input  MEMA_WE,
  input  MBRZ_OE,
  input  MBRA_OE,
  input  MBRB_OE,
  input  MBRZ_WE,
  input  MBRA_WE,
  input  MBRB_WE,
  input  REG8_WE,
  input  REG7_WE,
  input  REG6_WE,
  input  REG5_WE,
  input  REG4_WE,
  input  REG3_WE,
  input  REG2_WE,
  input  REG1_WE,
  input  INST_SPLITTER_WE,
  input  MARB_WE,
  input  MARA_WE,
  input  MARZ_WE,
  input  INSTMEM_OE,
  input  SYSMEM_OE,
  input  MEMB_OE,
  input  MEMA_OE,
  input  OUTPUT_REG_WE,
  input  REG_1_OE,
  input  REG_3_OE,
  input  REG_5_OE,
  input  REG_7_OE,
  input  REG_2_OE,
  input  REG_4_OE,
  input  REG_6_OE,
  input  REG_8_OE,
  input  BLOCK_COUNTER_LOAD_ON,
  input  BLOCK_COUNTER_INC
);

  wire Clk_out, instruction_splitter_1_flag, PROGRAM_COUNTER_carry;
  wire [3:0] counter_1_q;
  wire [4:0] block_incrementer_1_to_mar_a, block_incrementer_1_to_mar_b, controlled_buffer_5_out, MAR_A_q,
       MAR_B_q, MAR_Zero_q, PROGRAM_COUNTER_q, register_5_q;
  wire [7:0] mat_mult_1_p1, mat_mult_1_p2, mat_mult_1_p3, mat_mult_1_p4, mat_mult_1_p5, mat_mult_1_p6,
       mat_mult_1_p7, mat_mult_1_p8;
  wire [15:0] alu_1_result, bit_extender_1_out, bit_extender_2_out, bit_extender_3_out, bit_extender_4_out,
       bit_extender_5_out, bit_extender_6_out, bit_extender_7_out, bit_extender_8_out,
       controlled_buffer_1_out, controlled_buffer_6_out, controlled_buffer_7_out, controlled_buffer_8_out,
       controlled_buffer_9_out, mat_mult_1_p9, mat_mult_1_p10, mat_mult_1_p11, mat_mult_1_p12, MBR_A_q,
       MBR_B_q, MBR_Z_q, OUTPUT_REG_q, RAM_A_dout, RAM_B_dout, register_1_q, register_2_q, register_3_q,
       register_4_q;
  wire [47:0] ROM_PCU_data;

  assign bit_extender_1_out = {{8{mat_mult_1_p8[7]}}, mat_mult_1_p8};  // Bit_Extender bit_extender_1
  assign bit_extender_2_out = {{8{mat_mult_1_p7[7]}}, mat_mult_1_p7};  // Bit_Extender bit_extender_2
  assign bit_extender_3_out = {{8{mat_mult_1_p6[7]}}, mat_mult_1_p6};  // Bit_Extender bit_extender_3
  assign bit_extender_4_out = {{8{mat_mult_1_p3[7]}}, mat_mult_1_p3};  // Bit_Extender bit_extender_4
  assign bit_extender_5_out = {{8{mat_mult_1_p4[7]}}, mat_mult_1_p4};  // Bit_Extender bit_extender_5
  assign bit_extender_6_out = {{8{mat_mult_1_p1[7]}}, mat_mult_1_p1};  // Bit_Extender bit_extender_6
  assign bit_extender_7_out = {{8{mat_mult_1_p5[7]}}, mat_mult_1_p5};  // Bit_Extender bit_extender_7
  assign bit_extender_8_out = {{8{mat_mult_1_p2[7]}}, mat_mult_1_p2};  // Bit_Extender bit_extender_8
  BLOCK_INCREMENTER block_incrementer_1 (
    .ADD_A(MAR_A_q), .CLOCK(Clk_out), .COUNTER_LOAD_ON(ROM_PCU_data[7]),
    .COUNTER_INC_ON_ENABLE(ROM_PCU_data[6]), .ADD_B(MAR_B_q), .TO_MAR_A(block_incrementer_1_to_mar_a),
    .TO_MAR_B(block_incrementer_1_to_mar_b));
  // MAT_MULT mat_mult_1: pin names not known; wires that end beside it: mat_mult_1_p1, mat_mult_1_p2, mat_mult_1_p3, mat_mult_1_p4, mat_mult_1_p5, mat_mult_1_p6, mat_mult_1_p7, mat_mult_1_p8, mat_mult_1_p9, mat_mult_1_p10, mat_mult_1_p11, mat_mult_1_p12
  ALU alu_1 (
    .A(bit_extender_6_out), .B(bit_extender_8_out), .Flag(instruction_splitter_1_flag),
    .Opcode(controlled_buffer_5_out), .RESULT(alu_1_result));  // open: OVERFLOW_OUT
  // Probe on ROM_PCU_data[45]
  // Probe on ROM_PCU_data[43]
  Register #(.width(16)) register_1 (.D(mat_mult_1_p9), .Q(register_1_q));  // open: en, clk, clr
  Register #(.width(16)) register_2 (.D(mat_mult_1_p10), .Q(register_2_q));  // open: en, clk, clr
  Register #(.width(16)) register_3 (.D(mat_mult_1_p11), .Q(register_3_q));  // open: en, clk, clr
  Register #(.width(16)) register_4 (.D(mat_mult_1_p12), .Q(register_4_q));  // open: en, clk, clr
  Register #(.width(16)) OUTPUT_REG (
    .D(alu_1_result), .en(ROM_PCU_data[16]), .clk(Clk_out), .Q(OUTPUT_REG_q));  // open: clr
  Counter #(.max('h1f), .width(5)) PROGRAM_COUNTER (
    .clr(ROM_PCU_data[45]), .up(ROM_PCU_data[43]), .count(ROM_PCU_data[44]), .clk(Clk_out),
    .carry(PROGRAM_COUNTER_carry), .Q(PROGRAM_COUNTER_q));  // open: load, D
  Controlled_Buffer #(.width(16)) controlled_buffer_1 (.in(register_1_q), .out(controlled_buffer_1_out));  // open: en
  Controlled_Buffer #(.width(16)) controlled_buffer_2 (.in(register_2_q), .out(controlled_buffer_1_out));  // open: en
  Register #(.width(5)) register_5 (
    .D(controlled_buffer_5_out), .en(ROM_PCU_data[46]), .clk(Clk_out), .Q(register_5_q));  // open: clr
  Controlled_Buffer #(.width(16)) controlled_buffer_3 (.in(register_3_q), .out(controlled_buffer_1_out));  // open: en
  Controlled_Buffer #(.width(16)) controlled_buffer_4 (.in(register_4_q), .out(controlled_buffer_1_out));  // open: en
  // Probe on PROGRAM_COUNTER_carry
  assign controlled_buffer_5_out = ROM_PCU_data[47] ? {5{1'b0}} : 5'bz;  // Controlled_Buffer controlled_buffer_5
  Instruction_splitter instruction_splitter_1 (
    .Instruction(controlled_buffer_7_out), .Write_Enable(ROM_PCU_data[24]), .Clock(Clk_out),
    .Add_B(block_incrementer_1_to_mar_b), .Add_A(block_incrementer_1_to_mar_a),
    .Opcode(controlled_buffer_5_out), .Flag(instruction_splitter_1_flag));
  Register #(.width(5)) MAR_Zero (
    .D(PROGRAM_COUNTER_q), .en(ROM_PCU_data[21]), .clk(Clk_out), .Q(MAR_Zero_q));  // open: clr
  Register #(.width(5)) MAR_A (
    .D(block_incrementer_1_to_mar_a), .en(ROM_PCU_data[22]), .clk(Clk_out), .Q(MAR_A_q));  // open: clr
  REG_BANK_A reg_bank_a_1 (
    .REG_BANK_A_INPUT(controlled_buffer_8_out), .REG_1_WE(ROM_PCU_data[25]), .REG_1_OE(ROM_PCU_data[15]),
    .REG_2_WE(ROM_PCU_data[26]), .REG_2_OE(ROM_PCU_data[11]), .REG_3_WE(ROM_PCU_data[27]),
    .REG_3_OE(ROM_PCU_data[14]), .REG_4_WE(ROM_PCU_data[28]), .REG_4_OE(ROM_PCU_data[10]), .CLOCK(Clk_out),
    .OUTPUT_REG_1(bit_extender_6_out), .OUTPUT_REG_2(bit_extender_4_out), .OUTPUT_REG_3(bit_extender_2_out),
    .OUTPUT_REG_4(bit_extender_1_out));
  REG_BANK_B reg_bank_b_1 (
    .REG_BANK_B_INPUT(controlled_buffer_9_out), .REG_5_WE(ROM_PCU_data[29]), .REG_5_OE(ROM_PCU_data[13]),
    .REG_6_WE(ROM_PCU_data[30]), .REG_6_OE(ROM_PCU_data[9]), .REG_7_WE(ROM_PCU_data[31]),
    .REG_7_OE(ROM_PCU_data[12]), .REG_8_WE(ROM_PCU_data[32]), .REG_8_OE(ROM_PCU_data[8]), .CLOCK(Clk_out),
    .OUTPUT_REG_5(bit_extender_8_out), .OUTPUT_REG_6(bit_extender_7_out), .OUTPUT_REG_7(bit_extender_5_out),
    .OUTPUT_REG_8(bit_extender_3_out));
  Controlled_Buffer #(.width(16)) controlled_buffer_6 (
    .in(controlled_buffer_1_out), .out(controlled_buffer_6_out));  // open: en
  Register #(.width(5)) MAR_B (
    .D(block_incrementer_1_to_mar_b), .en(ROM_PCU_data[23]), .clk(Clk_out), .Q(MAR_B_q));  // open: clr
  Clock Clk (.out(Clk_out));
  Register #(.width(16)) MBR_Z (
    .D(controlled_buffer_6_out), .en(ROM_PCU_data[35]), .clk(Clk_out), .Q(MBR_Z_q));  // open: clr
  Register #(.width(16)) MBR_A (.D(RAM_A_dout), .en(ROM_PCU_data[34]), .clk(Clk_out), .Q(MBR_A_q));  // open: clr
  Register #(.width(16)) MBR_B (.D(RAM_B_dout), .en(ROM_PCU_data[33]), .clk(Clk_out), .Q(MBR_B_q));  // open: clr
  assign controlled_buffer_7_out = ROM_PCU_data[38] ? MBR_Z_q : 16'bz;  // Controlled_Buffer controlled_buffer_7
  assign controlled_buffer_8_out = ROM_PCU_data[37] ? MBR_A_q : 16'bz;  // Controlled_Buffer controlled_buffer_8
  assign controlled_buffer_9_out = ROM_PCU_data[36] ? MBR_B_q : 16'bz;  // Controlled_Buffer controlled_buffer_9
  RAM #(.addrWidth(5), .dataWidth(16)) inst_mem (
    .addr(MAR_Zero_q), .oe(ROM_PCU_data[20]), .clk(Clk_out), .din(controlled_buffer_7_out),
    .dout(controlled_buffer_6_out));  // open: we
  RAM #(.addrWidth(5), .dataWidth(16)) RAM_A (
    .addr(MAR_A_q), .we(ROM_PCU_data[39]), .oe(ROM_PCU_data[17]), .clk(Clk_out),
    .din(controlled_buffer_8_out), .dout(RAM_A_dout));
  RAM #(.addrWidth(5), .dataWidth(16)) SYS_MEM (
    .addr(MAR_Zero_q), .we(ROM_PCU_data[41]), .oe(ROM_PCU_data[19]), .clk(Clk_out), .din(OUTPUT_REG_q),
    .dout(controlled_buffer_6_out));
  RAM #(.addrWidth(5), .dataWidth(16)) RAM_B (
    .addr(MAR_B_q), .we(ROM_PCU_data[42]), .oe(ROM_PCU_data[18]), .clk(Clk_out),
    .din(controlled_buffer_9_out), .dout(RAM_B_dout));
  ROM #(.dataWidth(48)) ROM_PCU (.addr({register_5_q[3:0], counter_1_q}), .data(ROM_PCU_data));
  Counter #(.max('hf), .width(4)) counter_1 (
    .up(1'b1), .count(1'b1), .clk(Clk_out), .Q(counter_1_q));  // open: clr, load, D, carry

  // Notes on the sheet:
  //   contents of ROM_PCU (hex, n*v repeats v):
  //   c800002000 1800001000 808000000 840010000 80000c000 4800000000 800000600 806000000 830220000 8000001
  //   a000000 5*0 48000020 18000010 8080000 8400100 80000c0 48000000 8000006 8060000 8302200 8000001
  //   a000000 5*0 48000020 18000010 8080000 8400100 80000c0 48000000 8000006 8060000 8302200 8000001
  //   a000000 5*0 48000020 18000010 8080000 8400100 80000c0 48000000 8000006 8060000 8302200 8000001
  //   a000000 5*0 48000020 18000010 8080000 8400100 80000c0 48000000 8000006 8060000 8302200 8000001
  //   a000000 5*0 48000020 18000010 8080000 8400100 80000c0 48000000 8000006 8060000 8302200 8000001
  //   a000000 5*0 48000020 18000010 8080000 8400100 80000c0 48000000 8000006 8060000 8302200 8000001
  //   a000000 5*0 48000020 18000010 8080000 8400100 80000c0 48000000 8000006 8060000 8302200 8000001
  //   a000000
endmodule

module REG_BANK_A (
  input  [15:0] REG_BANK_A_INPUT,
  input  REG_1_WE,
  input  REG_1_OE,
  input  REG_2_WE,
  input  REG_2_OE,
  input  REG_3_WE,
  input  REG_3_OE,
  input  REG_4_WE,
  input  REG_4_OE,
  input  CLOCK,
  output [15:0] OUTPUT_REG_1,
  output [15:0] OUTPUT_REG_2,
  output [15:0] OUTPUT_REG_3,
  output [15:0] OUTPUT_REG_4
);

  wire [15:0] REG_1_q, REG_2_q, REG_3_q, REG_4_q;

  Register #(.width(16)) REG_2 (.D(REG_BANK_A_INPUT), .en(REG_2_WE), .clk(CLOCK), .Q(REG_2_q));  // open: clr
  Register #(.width(16)) REG_3 (.D(REG_BANK_A_INPUT), .en(REG_3_WE), .clk(CLOCK), .Q(REG_3_q));  // open: clr
  Register #(.width(16)) REG_4 (.D(REG_BANK_A_INPUT), .en(REG_4_WE), .clk(CLOCK), .Q(REG_4_q));  // open: clr
  Register #(.width(16)) REG_1 (.D(REG_BANK_A_INPUT), .en(REG_1_WE), .clk(CLOCK), .Q(REG_1_q));  // open: clr
  assign OUTPUT_REG_1 = REG_1_OE ? REG_1_q : 16'bz;  // Controlled_Buffer controlled_buffer_1
  assign OUTPUT_REG_2 = REG_2_OE ? REG_2_q : 16'bz;  // Controlled_Buffer controlled_buffer_2
  assign OUTPUT_REG_3 = REG_3_OE ? REG_3_q : 16'bz;  // Controlled_Buffer controlled_buffer_3
  assign OUTPUT_REG_4 = REG_4_OE ? REG_4_q : 16'bz;  // Controlled_Buffer controlled_buffer_4
endmodule

module BUS_TERMINUS (
  input  [15:0] DATA_A,
  input  TERMINAL_A_WE,
  input  CLOCK,
  input  [15:0] DATA_B,
  input  TERMINAL_B_WE,
  input  B_1,
  input  B_2,
  input  OE,
  output [15:0] TO_MBR_A,
  output [15:0] TO_MBR_Z_FROM_TERM_A,
  output [15:0] TO_MBRB,
  output [15:0] TO_MBR_Z_FROM_TERM_B
);

  wire and_1_out, and_2_out, decoder_bus_1_ram_a_or_ram_b, decoder_bus_1_sys_ram, not_1_out;
  wire [15:0] TERMINAL_A_q, TERMINAL_B_q;

  DECODER_BUS decoder_bus_1 (
    .A(B_1), .B(B_2), .RAM_A_OR_RAM_B(decoder_bus_1_ram_a_or_ram_b), .SYS_RAM(decoder_bus_1_sys_ram));
  and and_1 (and_1_out, OE, decoder_bus_1_ram_a_or_ram_b);
  and and_2 (and_2_out, decoder_bus_1_sys_ram, OE);
  Register #(.width(16)) TERMINAL_A (.D(DATA_A), .en(TERMINAL_A_WE), .clk(CLOCK), .Q(TERMINAL_A_q));  // open: clr
  Register #(.width(16)) TERMINAL_B (.D(DATA_B), .en(TERMINAL_B_WE), .clk(CLOCK), .Q(TERMINAL_B_q));  // open: clr
  assign TO_MBR_A = and_1_out ? TERMINAL_A_q : 16'bz;  // Controlled_Buffer controlled_buffer_1
  assign TO_MBR_Z_FROM_TERM_A = and_2_out ? TERMINAL_A_q : 16'bz;  // Controlled_Buffer controlled_buffer_2
  assign TO_MBRB = and_1_out ? TERMINAL_B_q : 16'bz;  // Controlled_Buffer controlled_buffer_3
  not not_1 (not_1_out, and_2_out);
  assign TO_MBR_Z_FROM_TERM_B = not_1_out ? TERMINAL_B_q : 16'bz;  // Controlled_Buffer controlled_buffer_4
endmodule

module REG_BANK_B (
  input  [15:0] REG_BANK_B_INPUT,
  input  REG_5_WE,
  input  REG_5_OE,
  input  REG_6_WE,
  input  REG_6_OE,
  input  REG_7_WE,
  input  REG_7_OE,
  input  REG_8_WE,
  input  REG_8_OE,
  input  CLOCK,
  output [15:0] OUTPUT_REG_5,
  output [15:0] OUTPUT_REG_6,
  output [15:0] OUTPUT_REG_7,
  output [15:0] OUTPUT_REG_8
);

  wire [15:0] REG_5_q, REG_6_q, REG_7_q, REG_8_q;

  Register #(.width(16)) REG_6 (.D(REG_BANK_B_INPUT), .en(REG_6_WE), .clk(CLOCK), .Q(REG_6_q));  // open: clr
  Register #(.width(16)) REG_7 (.D(REG_BANK_B_INPUT), .en(REG_7_WE), .clk(CLOCK), .Q(REG_7_q));  // open: clr
  Register #(.width(16)) REG_8 (.D(REG_BANK_B_INPUT), .en(REG_8_WE), .clk(CLOCK), .Q(REG_8_q));  // open: clr
  Register #(.width(16)) REG_5 (.D(REG_BANK_B_INPUT), .en(REG_5_WE), .clk(CLOCK), .Q(REG_5_q));  // open: clr
  assign OUTPUT_REG_5 = REG_5_OE ? REG_5_q : 16'bz;  // Controlled_Buffer controlled_buffer_1
  assign OUTPUT_REG_6 = REG_6_OE ? REG_6_q : 16'bz;  // Controlled_Buffer controlled_buffer_2
  assign OUTPUT_REG_7 = REG_7_OE ? REG_7_q : 16'bz;  // Controlled_Buffer controlled_buffer_3
  assign OUTPUT_REG_8 = REG_8_OE ? REG_8_q : 16'bz;  // Controlled_Buffer controlled_buffer_4
endmodule

module DECODER_BUS (
  input  A,
  input  B,
  output RAM_A_OR_RAM_B,
  output SYS_RAM
);

  wire not_1_out, not_2_out;

  not not_1 (not_1_out, A);
  not not_2 (not_2_out, B);
  and and_1 (RAM_A_OR_RAM_B, not_1_out, B);
  and and_2 (SYS_RAM, A, not_2_out);
endmodule

module BLOCK_INCREMENTER (
  input  [4:0] ADD_A,
  input  CLOCK,
  input  COUNTER_LOAD_ON,
  input  COUNTER_INC_ON_ENABLE,
  input  [4:0] ADD_B,
  output [4:0] TO_MAR_A,
  output [4:0] TO_MAR_B
);

  Counter #(.max('hf), .width(5)) COUNTER_BLOCK_LOAD_A (
    .load(COUNTER_LOAD_ON), .up(1'b1), .count(COUNTER_INC_ON_ENABLE), .clk(CLOCK), .D(ADD_A), .Q(TO_MAR_A));  // open: clr, carry
  Counter #(.max('hf), .width(5)) COUNTER_BLOCK_LOAD_B (
    .load(COUNTER_LOAD_ON), .up(1'b1), .count(COUNTER_INC_ON_ENABLE), .clk(CLOCK), .D(ADD_B), .Q(TO_MAR_B));  // open: clr, carry
endmodule

module FINAL_DECODER (
  input  A,
  input  B,
  input  C,
  input  D,
  input  E,
  output RESERVED,
  output BLOCK_MOVE,
  output MEM_SWAP,
  output REG_SWAP,
  output BLOCK_LOAD,
  output BLOCK_STORE,
  output MOVE_TO_MEM_A,
  output MOVE_TO_MEM_B,
  output STORE,
  output STORE_OVERFLOW,
  output MAT_MULT
);

  wire not_1_out, not_2_out, not_3_out, not_4_out, not_5_out;

  not not_1 (not_1_out, A);
  not not_2 (not_2_out, B);
  not not_3 (not_3_out, C);
  not not_4 (not_4_out, D);
  not not_5 (not_5_out, E);
  and and_1 (RESERVED, not_2_out, not_4_out, not_5_out);
  and and_2 (BLOCK_MOVE, not_2_out, D, not_5_out);
  and and_3 (MEM_SWAP, not_2_out, not_4_out, E);
  and and_4 (REG_SWAP, not_2_out, D, not_5_out);
  and and_5 (BLOCK_LOAD, not_2_out, D, E);
  and and_6 (BLOCK_STORE, B, not_4_out, not_5_out);
  and and_7 (MOVE_TO_MEM_A, not_1_out, B, C, D, E);
  and and_8 (MOVE_TO_MEM_B, A, B, C, D, E);
  and and_9 (STORE, not_1_out, not_2_out, C, not_4_out, not_5_out);
  and and_10 (STORE_OVERFLOW, A, not_2_out, C, not_4_out, not_5_out);
  and and_11 (MAT_MULT, B, not_4_out, E);
endmodule

module MBRS (
  input  [15:0] TO_MBR_Z,
  input  CLOCK,
  input  MBR_Z_WE,
  input  MBR_Z_OE,
  input  [15:0] TO_MBR_A,
  input  MBR_A_WE,
  input  MBR_A_OE,
  input  MBR_B_WE,
  input  MBR_B_OE,
  input  [15:0] TO_MBR_B,
  output [15:0] OUTPUT_MBR_Z,
  output [15:0] OUTPUT_MBR_A,
  output [15:0] OUTPUT_MBR_B
);

  wire [15:0] MBR_A_q, MBR_B_q, MBR_Z_q;

  Register #(.width(16)) MBR_Z (.D(TO_MBR_Z), .en(MBR_Z_WE), .clk(CLOCK), .Q(MBR_Z_q));  // open: clr
  Register #(.width(16)) MBR_A (.D(TO_MBR_A), .en(MBR_A_WE), .clk(CLOCK), .Q(MBR_A_q));  // open: clr
  Register #(.width(16)) MBR_B (.D(TO_MBR_B), .en(MBR_B_WE), .clk(CLOCK), .Q(MBR_B_q));  // open: clr
  assign OUTPUT_MBR_Z = MBR_Z_OE ? MBR_Z_q : 16'bz;  // Controlled_Buffer controlled_buffer_1
  assign OUTPUT_MBR_A = MBR_A_OE ? MBR_A_q : 16'bz;  // Controlled_Buffer controlled_buffer_2
  assign OUTPUT_MBR_B = MBR_B_OE ? MBR_B_q : 16'bz;  // Controlled_Buffer controlled_buffer_3
endmodule

module temp_useless (
  input  OPCODE_INIT_CB,
  input  OPCODE_REG_WE,
  input  COUNTER_RESET,
  input  COUNTER_INC_BY1,
  input  COUNTER_INC_ON,
  input  MEMB_WE,
  input  SYSMEM_WE,
  input  MEMA_WE,
  input  BUS_TERMINUS_OE,
  input  MBRZ_OE,
  input  MBRA_OE,
  input  MBRB_OE,
  input  MBRZ_WE,
  input  MBRA_WE,
  input  MBRB_WE,
  input  REG8_WE,
  input  REG7_WE,
  input  REG6_WE,
  input  REG5_WE,
  input  REG4_WE,
  input  REG3_WE,
  input  REG2_WE,
  input  REG1_WE,
  input  INST_SPLITTER_WE,
  input  MARB_WE,
  input  MARA_WE,
  input  MARZ_WE,
  input  INSTMEM_OE,
  input  SYSMEM_OE,
  input  MEMB_OE,
  input  MEMA_OE,
  input  OUTPUT_REG_WE,
  input  REG_1_OE,
  input  REG_3_OE,
  input  REG_5_OE,
  input  REG_7_OE,
  input  REG_2_OE,
  input  REG_4_OE,
  input  REG_6_OE,
  input  REG_8_OE,
  input  BLOCK_COUNTER_LOAD_ON,
  input  BLOCK_COUNTER_INC,
  input  MAT_MULT_RESULTS_ALL_REG_WE,
  output NOP,
  output out_45
);

  wire Clk_out, controlled_buffer_5_out, final_decoder_1_store, final_decoder_1_store_overflow,
       instruction_splitter_1_flag, nop_halt_1_halt, not_1_out, PROGRAM_COUNTER_carry;
  wire [3:0] counter_1_q;
  wire [4:0] block_incrementer_1_to_mar_a, block_incrementer_1_to_mar_b, controlled_buffer_3_out,
       mars_1_output_mar_a, mars_1_output_mar_b, mars_1_output_mar_z, PROGRAM_COUNTER_q, register_1_q;
  wire [15:0] alu_1_overflow_out, alu_1_result, bus_terminus_1_to_mbr_a, bus_terminus_1_to_mbr_z_from_term_a,
       controlled_buffer_1_out, controlled_buffer_4_out, mat_mult_1_prod1_topleft, mat_mult_1_prod2_topright,
       mat_mult_1_prod3_bottomleft, mat_mult_1_prod4_bottomright, matmult_results_1_output_prod1_topleft,
       mbrs_1_output_mbr_a, mbrs_1_output_mbr_b, mbrs_1_output_mbr_z, OUTPUT_REG_q, OVERFLOW_REG_q,
       reg_bank_a_1_output_reg_1, reg_bank_a_1_output_reg_2, reg_bank_a_1_output_reg_3,
       reg_bank_a_1_output_reg_4, reg_bank_b_1_output_reg_5, reg_bank_b_1_output_reg_6,
       reg_bank_b_1_output_reg_7, reg_bank_b_1_output_reg_8;
  wire [46:0] ROM_PCU_data;

  FINAL_DECODER final_decoder_1 (
    .A(instruction_splitter_1_flag), .B(controlled_buffer_3_out[3]), .C(controlled_buffer_3_out[2]),
    .D(controlled_buffer_3_out[1]), .E(controlled_buffer_3_out[0]), .RESERVED(out_45),
    .STORE(final_decoder_1_store), .STORE_OVERFLOW(final_decoder_1_store_overflow));  // open: BLOCK_MOVE, MEM_SWAP, REG_SWAP, BLOCK_LOAD, BLOCK_STORE, MOVE_TO_MEM_A, MOVE_TO_MEM_B, MAT_MULT
  BLOCK_INCREMENTER block_incrementer_1 (
    .ADD_A(mars_1_output_mar_a), .CLOCK(controlled_buffer_5_out), .COUNTER_LOAD_ON(ROM_PCU_data[40]),
    .COUNTER_INC_ON_ENABLE(ROM_PCU_data[41]), .ADD_B(mars_1_output_mar_b),
    .TO_MAR_A(block_incrementer_1_to_mar_a), .TO_MAR_B(block_incrementer_1_to_mar_b));
  MAT_MULT mat_mult_1 (
    .REG_1(reg_bank_a_1_output_reg_1), .REG_5(reg_bank_b_1_output_reg_5), .REG_2(reg_bank_a_1_output_reg_2),
    .REG_7(reg_bank_b_1_output_reg_7), .REG_6(reg_bank_b_1_output_reg_6), .REG_8(reg_bank_b_1_output_reg_8),
    .REG_3(reg_bank_a_1_output_reg_3), .REG_4(reg_bank_a_1_output_reg_4),
    .PROD1_TOPLEFT(mat_mult_1_prod1_topleft), .PROD2_TOPRIGHT(mat_mult_1_prod2_topright),
    .PROD3_BOTTOMLEFT(mat_mult_1_prod3_bottomleft), .PROD4_BOTTOMRIGHT(mat_mult_1_prod4_bottomright));
  ALU alu_1 (
    .A(reg_bank_a_1_output_reg_1), .B(reg_bank_b_1_output_reg_5), .Flag(instruction_splitter_1_flag),
    .Opcode(controlled_buffer_3_out), .RESULT(alu_1_result), .OVERFLOW_OUT(alu_1_overflow_out));
  NOP_HALT nop_halt_1 (
    .A(instruction_splitter_1_flag), .B(controlled_buffer_3_out[3]), .C(controlled_buffer_3_out[2]),
    .D(controlled_buffer_3_out[1]), .E(controlled_buffer_3_out[0]), .NOP(NOP), .HALT(nop_halt_1_halt));
  // Probe on ROM_PCU_data[2]
  // Probe on ROM_PCU_data[4]
  Register #(.width(16)) OUTPUT_REG (
    .D(alu_1_result), .en(ROM_PCU_data[31]), .clk(controlled_buffer_5_out), .Q(OUTPUT_REG_q));  // open: clr
  Register #(.width(16)) OVERFLOW_REG (
    .D(alu_1_overflow_out), .en(ROM_PCU_data[31]), .clk(controlled_buffer_5_out), .Q(OVERFLOW_REG_q));  // open: clr
  Counter #(.max('h1f), .width(5)) PROGRAM_COUNTER (
    .clr(ROM_PCU_data[2]), .up(ROM_PCU_data[4]), .count(ROM_PCU_data[3]), .clk(controlled_buffer_5_out),
    .carry(PROGRAM_COUNTER_carry), .Q(PROGRAM_COUNTER_q));  // open: load, D
  assign controlled_buffer_1_out = final_decoder_1_store ? OUTPUT_REG_q : 16'bz;  // Controlled_Buffer controlled_buffer_1
  Register #(.width(5)) register_1 (
    .D(controlled_buffer_3_out), .en(ROM_PCU_data[1]), .clk(controlled_buffer_5_out), .Q(register_1_q));  // open: clr
  assign controlled_buffer_1_out = final_decoder_1_store_overflow ? OVERFLOW_REG_q : 16'bz;  // Controlled_Buffer controlled_buffer_2
  MATMULT_RESULTS matmult_results_1 (
    .CLOCK(controlled_buffer_5_out), .PROD1_TOPLEFT(mat_mult_1_prod1_topleft),
    .PROD1_TOPLEFT_WE(ROM_PCU_data[42]), .PROD1_TOPLEFT_OE(ROM_PCU_data[46]),
    .PROD2_TOPRIGHT(mat_mult_1_prod2_topright), .PROD2_TOPRIGHT_WE(ROM_PCU_data[42]),
    .PROD2_TOPRIGHT_OE(ROM_PCU_data[45]), .PROD3_BOTTOMLEFT(mat_mult_1_prod3_bottomleft),
    .PROD3_BOTTOMLEFT_WE(ROM_PCU_data[42]), .PROD3_BOTTOMLEFT_OE(ROM_PCU_data[44]),
    .PROD4_BOTTOMRIGHT(mat_mult_1_prod4_bottomright), .PROD4_BOTTOMRIGHT_WE(ROM_PCU_data[42]),
    .PROD4_BOTTOMRIGHT_OE(ROM_PCU_data[43]), .OUTPUT_PROD1_TOPLEFT(matmult_results_1_output_prod1_topleft),
    .OUTPUT_PROD2_TOPRIGHT(matmult_results_1_output_prod1_topleft),
    .OUTPUT_PROD3_BOTTOMLEFT(matmult_results_1_output_prod1_topleft),
    .OUTPUT_PROD4_BOTTOMRIGHT(matmult_results_1_output_prod1_topleft));
  // Probe on PROGRAM_COUNTER_carry
  assign controlled_buffer_3_out = ROM_PCU_data[0] ? {5{1'b0}} : 5'bz;  // Controlled_Buffer controlled_buffer_3
  Instruction_splitter instruction_splitter_1 (
    .Instruction(mbrs_1_output_mbr_z), .Write_Enable(ROM_PCU_data[23]), .Clock(controlled_buffer_5_out),
    .Add_B(block_incrementer_1_to_mar_a), .Add_A(block_incrementer_1_to_mar_b),
    .Opcode(controlled_buffer_3_out), .Flag(instruction_splitter_1_flag));
  Controlled_Buffer #(.width(16)) controlled_buffer_4 (
    .in(matmult_results_1_output_prod1_topleft), .out(controlled_buffer_4_out));  // open: en
  BUS_TERMINUS bus_terminus_1 (
    .CLOCK(controlled_buffer_5_out), .DATA_B(controlled_buffer_1_out), .OE(ROM_PCU_data[7]),
    .TO_MBR_A(bus_terminus_1_to_mbr_a), .TO_MBR_Z_FROM_TERM_A(bus_terminus_1_to_mbr_z_from_term_a),
    .TO_MBRB(controlled_buffer_4_out));  // open: DATA_A, TERMINAL_A_WE, TERMINAL_B_WE, B_1, B_2, TO_MBR_Z_FROM_TERM_B
  MARS mars_1 (
    .TO_MAR_Z(PROGRAM_COUNTER_q), .CLOCK(controlled_buffer_5_out), .MAR_Z_WE(ROM_PCU_data[26]),
    .TO_MAR_A(block_incrementer_1_to_mar_a), .MAR_A_WE(ROM_PCU_data[25]), .MAR_B_WE(ROM_PCU_data[24]),
    .TO_MAR_B(block_incrementer_1_to_mar_b), .OUTPUT_MAR_Z(mars_1_output_mar_z),
    .OUTPUT_MAR_A(mars_1_output_mar_a), .OUTPUT_MAR_B(mars_1_output_mar_b));
  REG_BANK_A reg_bank_a_1 (
    .REG_BANK_A_INPUT(mbrs_1_output_mbr_a), .REG_1_WE(ROM_PCU_data[22]), .REG_1_OE(ROM_PCU_data[32]),
    .REG_2_WE(ROM_PCU_data[21]), .REG_2_OE(ROM_PCU_data[36]), .REG_3_WE(ROM_PCU_data[20]),
    .REG_3_OE(ROM_PCU_data[33]), .REG_4_WE(ROM_PCU_data[19]), .REG_4_OE(ROM_PCU_data[37]),
    .CLOCK(controlled_buffer_5_out), .OUTPUT_REG_1(reg_bank_a_1_output_reg_1),
    .OUTPUT_REG_2(reg_bank_a_1_output_reg_2), .OUTPUT_REG_3(reg_bank_a_1_output_reg_3),
    .OUTPUT_REG_4(reg_bank_a_1_output_reg_4));
  REG_BANK_B reg_bank_b_1 (
    .REG_BANK_B_INPUT(mbrs_1_output_mbr_b), .REG_5_WE(ROM_PCU_data[18]), .REG_5_OE(ROM_PCU_data[34]),
    .REG_6_WE(ROM_PCU_data[17]), .REG_6_OE(ROM_PCU_data[38]), .REG_7_WE(ROM_PCU_data[16]),
    .REG_7_OE(ROM_PCU_data[35]), .REG_8_WE(ROM_PCU_data[15]), .REG_8_OE(ROM_PCU_data[39]),
    .CLOCK(controlled_buffer_5_out), .OUTPUT_REG_5(reg_bank_b_1_output_reg_5),
    .OUTPUT_REG_6(reg_bank_b_1_output_reg_6), .OUTPUT_REG_7(reg_bank_b_1_output_reg_7),
    .OUTPUT_REG_8(reg_bank_b_1_output_reg_8));
  assign controlled_buffer_5_out = not_1_out ? Clk_out : 1'bz;  // Controlled_Buffer controlled_buffer_5
  not not_1 (not_1_out, nop_halt_1_halt);
  Clock Clk (.out(Clk_out));
  assign controlled_buffer_5_out = not_1_out ? Clk_out : 1'bz;  // Controlled_Buffer controlled_buffer_6
  MBRS mbrs_1 (
    .TO_MBR_Z(controlled_buffer_4_out), .CLOCK(controlled_buffer_5_out), .MBR_Z_WE(ROM_PCU_data[12]),
    .MBR_Z_OE(ROM_PCU_data[9]), .TO_MBR_A(bus_terminus_1_to_mbr_a), .MBR_A_WE(ROM_PCU_data[13]),
    .MBR_A_OE(ROM_PCU_data[10]), .MBR_B_WE(ROM_PCU_data[14]), .MBR_B_OE(ROM_PCU_data[11]),
    .TO_MBR_B(bus_terminus_1_to_mbr_z_from_term_a), .OUTPUT_MBR_Z(mbrs_1_output_mbr_z),
    .OUTPUT_MBR_A(mbrs_1_output_mbr_a), .OUTPUT_MBR_B(mbrs_1_output_mbr_b));
  RAM #(.addrWidth(5), .dataWidth(16)) inst_mem (
    .addr(mars_1_output_mar_z), .oe(ROM_PCU_data[27]), .clk(controlled_buffer_5_out),
    .din(mbrs_1_output_mbr_z), .dout(controlled_buffer_4_out));  // open: we
  RAM #(.addrWidth(5), .dataWidth(16)) RAM_A (
    .addr(mars_1_output_mar_a), .we(ROM_PCU_data[8]), .oe(ROM_PCU_data[30]), .clk(controlled_buffer_5_out),
    .din(mbrs_1_output_mbr_a), .dout(bus_terminus_1_to_mbr_a));
  RAM #(.addrWidth(5), .dataWidth(16)) SYS_MEM (
    .addr(mars_1_output_mar_z), .we(ROM_PCU_data[6]), .oe(ROM_PCU_data[28]), .clk(controlled_buffer_5_out),
    .din(mbrs_1_output_mbr_z), .dout(controlled_buffer_4_out));
  RAM #(.addrWidth(5), .dataWidth(16)) RAM_B (
    .addr(mars_1_output_mar_b), .we(ROM_PCU_data[5]), .oe(ROM_PCU_data[29]), .clk(controlled_buffer_5_out),
    .din(mbrs_1_output_mbr_b), .dout(bus_terminus_1_to_mbr_z_from_term_a));
  ROM #(.dataWidth(47)) ROM_PCU (.addr({register_1_q[3:0], counter_1_q}), .data(ROM_PCU_data));
  Counter #(.max('hf), .width(4)) counter_1 (
    .up(1'b1), .count(1'b1), .clk(controlled_buffer_5_out), .Q(counter_1_q));  // open: clr, load, D, carry

  // Notes on the sheet:
  //   contents of ROM_PCU (hex, n*v repeats v):
  //   c800002000 1800001000 808000000 840010000 80000c000 4800000000 800000600 806000000 830220000 8000001
  //   a000000 5*0 48000020 18000010 8080000 8400100 80000c0 48000000 8000006 8060000 8302200 8000001
  //   a000000 5*0 48000020 18000010 8080000 8400100 80000c0 48000000 8000006 8060000 8302200 8000001
  //   a000000 5*0 48000020 18000010 8080000 8400100 80000c0 48000000 8000006 8060000 8302200 8000001
  //   a000000 5*0 48000020 18000010 8080000 8400100 80000c0 48000000 8000006 8060000 8302200 8000001
  //   a000000 5*0 48000020 18000010 8080000 8400100 80000c0 48000000 8000006 8060000 8302200 8000001
  //   a000000 5*0 48000020 18000010 8080000 8400100 80000c0 48000000 8000006 8060000 8302200 8000001
  //   a000000 5*0 48000020 18000010 8080000 8400100 80000c0 48000000 8000006 8060000 8302200 8000001
  //   a000000
endmodule

module MARS (
  input  [4:0] TO_MAR_Z,
  input  CLOCK,
  input  MAR_Z_WE,
  input  [4:0] TO_MAR_A,
  input  MAR_A_WE,
  input  MAR_B_WE,
  input  [4:0] TO_MAR_B,
  output [4:0] OUTPUT_MAR_Z,
  output [4:0] OUTPUT_MAR_A,
  output [4:0] OUTPUT_MAR_B
);

  Register #(.width(5)) MAR_Z (.D(TO_MAR_Z), .en(MAR_Z_WE), .clk(CLOCK), .Q(OUTPUT_MAR_Z));  // open: clr
  Register #(.width(5)) MAR_A (.D(TO_MAR_A), .en(MAR_A_WE), .clk(CLOCK), .Q(OUTPUT_MAR_A));  // open: clr
  Register #(.width(5)) MAR_B (.D(TO_MAR_B), .en(MAR_B_WE), .clk(CLOCK), .Q(OUTPUT_MAR_B));  // open: clr
endmodule

module MATMULT_RESULTS (
  input  CLOCK,
  input  [15:0] PROD1_TOPLEFT,
  input  PROD1_TOPLEFT_WE,
  input  PROD1_TOPLEFT_OE,
  input  [15:0] PROD2_TOPRIGHT,
  input  PROD2_TOPRIGHT_WE,
  input  PROD2_TOPRIGHT_OE,
  input  [15:0] PROD3_BOTTOMLEFT,
  input  PROD3_BOTTOMLEFT_WE,
  input  PROD3_BOTTOMLEFT_OE,
  input  [15:0] PROD4_BOTTOMRIGHT,
  input  PROD4_BOTTOMRIGHT_WE,
  input  PROD4_BOTTOMRIGHT_OE,
  output [15:0] OUTPUT_PROD1_TOPLEFT,
  output [15:0] OUTPUT_PROD2_TOPRIGHT,
  output [15:0] OUTPUT_PROD3_BOTTOMLEFT,
  output [15:0] OUTPUT_PROD4_BOTTOMRIGHT
);

  wire [15:0] PROD1_TOPLEFT_REG_q, PROD2_TOPRIGHT_REG_q, PROD3_BOTTOMLEFT_REG_q, PROD4_BOTTOMRIGHT_REG_q;

  Register #(.width(16)) PROD2_TOPRIGHT_REG (
    .D(PROD2_TOPRIGHT), .en(PROD2_TOPRIGHT_WE), .clk(CLOCK), .Q(PROD2_TOPRIGHT_REG_q));  // open: clr
  Register #(.width(16)) PROD1_TOPLEFT_REG (
    .D(PROD1_TOPLEFT), .en(PROD1_TOPLEFT_WE), .clk(CLOCK), .Q(PROD1_TOPLEFT_REG_q));  // open: clr
  Register #(.width(16)) PROD3_BOTTOMLEFT_REG (
    .D(PROD3_BOTTOMLEFT), .en(PROD3_BOTTOMLEFT_WE), .clk(CLOCK), .Q(PROD3_BOTTOMLEFT_REG_q));  // open: clr
  Register #(.width(16)) PROD4_BOTTOMRIGHT_REG (
    .D(PROD4_BOTTOMRIGHT), .en(PROD4_BOTTOMRIGHT_WE), .clk(CLOCK), .Q(PROD4_BOTTOMRIGHT_REG_q));  // open: clr
  assign OUTPUT_PROD1_TOPLEFT = PROD1_TOPLEFT_OE ? PROD1_TOPLEFT_REG_q : 16'bz;  // Controlled_Buffer controlled_buffer_1
  assign OUTPUT_PROD2_TOPRIGHT = PROD2_TOPRIGHT_OE ? PROD2_TOPRIGHT_REG_q : 16'bz;  // Controlled_Buffer controlled_buffer_2
  assign OUTPUT_PROD4_BOTTOMRIGHT = PROD4_BOTTOMRIGHT_OE ? PROD4_BOTTOMRIGHT_REG_q : 16'bz;  // Controlled_Buffer controlled_buffer_3
  assign OUTPUT_PROD3_BOTTOMLEFT = PROD3_BOTTOMLEFT_OE ? PROD3_BOTTOMLEFT_REG_q : 16'bz;  // Controlled_Buffer controlled_buffer_4
endmodule

module BLOCK_MOVE (
  input  INST_RAM_WE,
  input  INST_RAM_OE,
  input  SYS_RAM_WE,
  input  SYS_RAM_OE,
  input  MAR_Z_WE,
  input  MAR_A_WE,
  input  MAR_B_WE,
  input  MBR_Z_WE,
  input  MBR_Z_OE,
  input  MBR_A_WE,
  input  MBR_A_OE,
  input  MBR_B_WE,
  input  MBR_B_OE,
  input  COUNTER_INC_ON,
  input  COUNTER_INC_BY_1,
  input  REG_5_WE,
  input  REG_5_OE,
  input  REG_6_WE,
  input  REG_6_OE,
  input  REG_7_WE,
  input  REG_7_OE,
  input  REG_8_WE,
  input  REG_8_OE,
  input  REG_1_WE,
  input  REG_1_OE,
  input  REG_2_WE,
  input  REG_2_OE,
  input  REG_3_WE,
  input  REG_3_OE,
  input  REG_4_WE,
  input  REG_4_OE,
  input  OVERFLOW_REG_WE,
  input  OUTPUT_REG_WE,
  input  OPCODE_REG_INIT_CB,
  input  OPCODE_REG_WE,
  input  INST_SPLITTER_WE,
  input  MATMULT_ALL_PRODS_WE,
  input  MATMULT_PROD1_OE,
  input  MATMULT_PROD2_OE,
  input  MATMULT_PROD3_OE,
  input  MATMULT_PROD4_OE,
  input  BLOCK_INCREMENTER_ON_ENABLE,
  input  BLOCK_LOAD_ON,
  input  RAM_B_WE,
  input  RAM_B_OE,
  input  RAM_A_WE,
  input  RAM_A_OE,
  input  ROM_CLK_COUNT_RESET,
  input  BLOCK_INCREMENTER_ADD_ALLOW,
  input  MARS_ALLOW,
  input  BLOCK_INCREMENTER_INC_ADD_ALLOW,
  input  TERMINAL_A_WE,
  input  TERMINAL_B_WE,
  input  B1,
  input  B2,
  input  TERMINUS_OE,
  output NOP,
  output BLOCK_LOAD,
  output RESERVED
);

  wire and_1_out, CLK_out, controlled_buffer_17_out, final_decoder_1_block_move, final_decoder_1_block_store,
       final_decoder_1_mat_mult, final_decoder_1_move_to_mem_a, final_decoder_1_move_to_mem_b,
       final_decoder_1_store, final_decoder_1_store_overflow, instruction_splitter_1_flag, nand_1_out,
       nand_2_out, nop_halt_1_halt, nor_1_out, nor_2_out, nor_3_out, nor_4_out, not_1_out, not_2_out,
       not_3_out, not_4_out, not_5_out, not_6_out, not_7_out, not_8_out, not_9_out, not_10_out, not_11_out,
       or_1_out, xor_1_out, xor_2_out;
  wire [3:0] ROM_CLOCK_COUNTER_q;
  wire [4:0] block_incrementer_1_to_mar_a, block_incrementer_1_to_mar_b, BLOCK_MOVE_COUNTER_DESTINATION_q,
       BLOCK_MOVE_COUNTER_SOURCE_q, BLOCK_STORE_COUNTER_q, controlled_buffer_1_out, controlled_buffer_3_out,
       controlled_buffer_4_out, controlled_buffer_5_out, controlled_buffer_6_out, controlled_buffer_21_out,
       controlled_buffer_23_out, controlled_buffer_30_out, controlled_buffer_32_out,
       controlled_buffer_34_out, controlled_buffer_38_out, controlled_buffer_39_out,
       instruction_splitter_1_add_a, instruction_splitter_1_add_b, instruction_splitter_1_opcode,
       mars_1_output_mar_a, mars_1_output_mar_b, mars_1_output_mar_z, OPCODE_REG_q, PROGRAM_COUNTER_q;
  wire [15:0] alu_1_overflow_out, alu_1_result, bus_terminus_1_to_mbr_a, bus_terminus_1_to_mbr_z_from_term_a,
       bus_terminus_1_to_mbrb, controlled_buffer_8_out, controlled_buffer_9_out, controlled_buffer_10_out,
       controlled_buffer_11_out, controlled_buffer_13_out, controlled_buffer_14_out,
       controlled_buffer_15_out, controlled_buffer_16_out, controlled_buffer_25_out,
       controlled_buffer_31_out, INST_RAM_dout, mat_mult_1_prod1_topleft, mat_mult_1_prod2_topright,
       mat_mult_1_prod3_bottomleft, mat_mult_1_prod4_bottomright, matmult_results_1_output_prod1_topleft,
       mbrs_1_output_mbr_a, mbrs_1_output_mbr_b, mbrs_1_output_mbr_z, OUTPUT_REG_q, OVERFLOW_REG_q,
       RAM_A_dout, RAM_B_dout, reg_bank_a_1_output_reg_1, reg_bank_a_1_output_reg_2,
       reg_bank_a_1_output_reg_3, reg_bank_a_1_output_reg_4, reg_bank_b_1_output_reg_5,
       reg_bank_b_1_output_reg_6, reg_bank_b_1_output_reg_7, reg_bank_b_1_output_reg_8;
  wire [55:0] ROM_PCU_data;

  not not_1 (not_1_out, ROM_PCU_data[33]);
  FINAL_DECODER final_decoder_1 (
    .A(instruction_splitter_1_flag), .B(instruction_splitter_1_opcode[3]),
    .C(instruction_splitter_1_opcode[2]), .D(instruction_splitter_1_opcode[1]),
    .E(instruction_splitter_1_opcode[0]), .RESERVED(RESERVED), .BLOCK_MOVE(final_decoder_1_block_move),
    .BLOCK_LOAD(BLOCK_LOAD), .BLOCK_STORE(final_decoder_1_block_store),
    .MOVE_TO_MEM_A(final_decoder_1_move_to_mem_a), .MOVE_TO_MEM_B(final_decoder_1_move_to_mem_b),
    .STORE(final_decoder_1_store), .STORE_OVERFLOW(final_decoder_1_store_overflow),
    .MAT_MULT(final_decoder_1_mat_mult));  // open: MEM_SWAP, REG_SWAP
  not not_2 (not_2_out, ROM_PCU_data[55]);
  assign controlled_buffer_1_out = not_1_out ? instruction_splitter_1_opcode : 5'bz;  // Controlled_Buffer controlled_buffer_1
  MATMULT_RESULTS matmult_results_1 (
    .CLOCK(controlled_buffer_17_out), .PROD1_TOPLEFT(mat_mult_1_prod1_topleft),
    .PROD1_TOPLEFT_WE(ROM_PCU_data[36]), .PROD1_TOPLEFT_OE(ROM_PCU_data[37]),
    .PROD2_TOPRIGHT(mat_mult_1_prod2_topright), .PROD2_TOPRIGHT_WE(ROM_PCU_data[36]),
    .PROD2_TOPRIGHT_OE(ROM_PCU_data[38]), .PROD3_BOTTOMLEFT(mat_mult_1_prod3_bottomleft),
    .PROD3_BOTTOMLEFT_WE(ROM_PCU_data[36]), .PROD3_BOTTOMLEFT_OE(ROM_PCU_data[39]),
    .PROD4_BOTTOMRIGHT(mat_mult_1_prod4_bottomright), .PROD4_BOTTOMRIGHT_WE(ROM_PCU_data[36]),
    .PROD4_BOTTOMRIGHT_OE(ROM_PCU_data[40]), .OUTPUT_PROD1_TOPLEFT(matmult_results_1_output_prod1_topleft),
    .OUTPUT_PROD2_TOPRIGHT(matmult_results_1_output_prod1_topleft),
    .OUTPUT_PROD3_BOTTOMLEFT(matmult_results_1_output_prod1_topleft),
    .OUTPUT_PROD4_BOTTOMRIGHT(matmult_results_1_output_prod1_topleft));
  Register #(.width(5)) OPCODE_REG (
    .D(controlled_buffer_1_out), .en(ROM_PCU_data[34]), .clk(controlled_buffer_17_out), .Q(OPCODE_REG_q));  // open: clr
  assign controlled_buffer_1_out = ROM_PCU_data[33] ? {5{1'b0}} : 5'bz;  // Controlled_Buffer controlled_buffer_2
  assign controlled_buffer_3_out = ROM_PCU_data[49] ? instruction_splitter_1_add_b : 5'bz;  // Controlled_Buffer controlled_buffer_3
  BUS_TERMINUS bus_terminus_1 (
    .DATA_A(mbrs_1_output_mbr_z), .TERMINAL_A_WE(ROM_PCU_data[51]), .CLOCK(controlled_buffer_17_out),
    .DATA_B(mbrs_1_output_mbr_z), .TERMINAL_B_WE(ROM_PCU_data[52]), .B_1(ROM_PCU_data[53]),
    .B_2(ROM_PCU_data[54]), .OE(ROM_PCU_data[55]), .TO_MBR_A(bus_terminus_1_to_mbr_a),
    .TO_MBR_Z_FROM_TERM_A(bus_terminus_1_to_mbr_z_from_term_a), .TO_MBRB(bus_terminus_1_to_mbrb),
    .TO_MBR_Z_FROM_TERM_B(bus_terminus_1_to_mbr_z_from_term_a));
  assign controlled_buffer_4_out = ROM_PCU_data[49] ? instruction_splitter_1_add_a : 5'bz;  // Controlled_Buffer controlled_buffer_4
  assign controlled_buffer_5_out = ROM_PCU_data[48] ? instruction_splitter_1_add_b : 5'bz;  // Controlled_Buffer controlled_buffer_5
  Instruction_splitter instruction_splitter_1 (
    .Instruction(mbrs_1_output_mbr_z), .Write_Enable(ROM_PCU_data[35]), .Clock(controlled_buffer_17_out),
    .Add_B(instruction_splitter_1_add_b), .Add_A(instruction_splitter_1_add_a),
    .Opcode(instruction_splitter_1_opcode), .Flag(instruction_splitter_1_flag));
  assign controlled_buffer_6_out = ROM_PCU_data[48] ? instruction_splitter_1_add_a : 5'bz;  // Controlled_Buffer controlled_buffer_6
  MAT_MULT mat_mult_1 (
    .REG_1(controlled_buffer_16_out), .REG_5(controlled_buffer_15_out), .REG_2(controlled_buffer_14_out),
    .REG_7(controlled_buffer_13_out), .REG_6(controlled_buffer_11_out), .REG_8(controlled_buffer_10_out),
    .REG_3(controlled_buffer_9_out), .REG_4(controlled_buffer_8_out),
    .PROD1_TOPLEFT(mat_mult_1_prod1_topleft), .PROD2_TOPRIGHT(mat_mult_1_prod2_topright),
    .PROD3_BOTTOMLEFT(mat_mult_1_prod3_bottomleft), .PROD4_BOTTOMRIGHT(mat_mult_1_prod4_bottomright));
  Register #(.width(16)) OVERFLOW_REG (
    .D(alu_1_overflow_out), .en(ROM_PCU_data[31]), .clk(controlled_buffer_17_out), .Q(OVERFLOW_REG_q));  // open: clr
  Register #(.width(16)) OUTPUT_REG (
    .D(alu_1_result), .en(ROM_PCU_data[32]), .clk(controlled_buffer_17_out), .Q(OUTPUT_REG_q));  // open: clr
  assign matmult_results_1_output_prod1_topleft = final_decoder_1_store_overflow ? OVERFLOW_REG_q : 16'bz;  // Controlled_Buffer controlled_buffer_7
  assign controlled_buffer_8_out = final_decoder_1_mat_mult ? reg_bank_a_1_output_reg_4 : 16'bz;  // Controlled_Buffer controlled_buffer_8
  assign controlled_buffer_9_out = final_decoder_1_mat_mult ? reg_bank_a_1_output_reg_3 : 16'bz;  // Controlled_Buffer controlled_buffer_9
  assign controlled_buffer_10_out = final_decoder_1_mat_mult ? reg_bank_b_1_output_reg_8 : 16'bz;  // Controlled_Buffer controlled_buffer_10
  assign controlled_buffer_11_out = final_decoder_1_mat_mult ? reg_bank_b_1_output_reg_6 : 16'bz;  // Controlled_Buffer controlled_buffer_11
  assign matmult_results_1_output_prod1_topleft = final_decoder_1_store ? OUTPUT_REG_q : 16'bz;  // Controlled_Buffer controlled_buffer_12
  NOP_HALT nop_halt_1 (
    .A(instruction_splitter_1_flag), .B(instruction_splitter_1_opcode[3]),
    .C(instruction_splitter_1_opcode[2]), .D(instruction_splitter_1_opcode[1]),
    .E(instruction_splitter_1_opcode[0]), .NOP(NOP), .HALT(nop_halt_1_halt));
  ALU alu_1 (
    .A(reg_bank_a_1_output_reg_1), .B(reg_bank_b_1_output_reg_5), .Flag(instruction_splitter_1_flag),
    .Opcode(instruction_splitter_1_opcode), .RESULT(alu_1_result), .OVERFLOW_OUT(alu_1_overflow_out));
  assign controlled_buffer_13_out = final_decoder_1_mat_mult ? reg_bank_b_1_output_reg_7 : 16'bz;  // Controlled_Buffer controlled_buffer_13
  assign controlled_buffer_14_out = final_decoder_1_mat_mult ? reg_bank_a_1_output_reg_2 : 16'bz;  // Controlled_Buffer controlled_buffer_14
  assign controlled_buffer_15_out = final_decoder_1_mat_mult ? reg_bank_b_1_output_reg_5 : 16'bz;  // Controlled_Buffer controlled_buffer_15
  assign controlled_buffer_16_out = final_decoder_1_mat_mult ? reg_bank_a_1_output_reg_1 : 16'bz;  // Controlled_Buffer controlled_buffer_16
  assign controlled_buffer_17_out = not_3_out ? CLK_out : 1'bz;  // Controlled_Buffer controlled_buffer_17
  Clock CLK (.out(CLK_out));
  assign controlled_buffer_17_out = not_3_out ? CLK_out : 1'bz;  // Controlled_Buffer controlled_buffer_18
  not not_3 (not_3_out, nop_halt_1_halt);
  REG_BANK_A reg_bank_a_1 (
    .REG_BANK_A_INPUT(mbrs_1_output_mbr_a), .REG_1_WE(ROM_PCU_data[23]), .REG_1_OE(ROM_PCU_data[24]),
    .REG_2_WE(ROM_PCU_data[25]), .REG_2_OE(ROM_PCU_data[26]), .REG_3_WE(ROM_PCU_data[27]),
    .REG_3_OE(ROM_PCU_data[28]), .REG_4_WE(ROM_PCU_data[29]), .REG_4_OE(ROM_PCU_data[30]),
    .CLOCK(controlled_buffer_17_out), .OUTPUT_REG_1(reg_bank_a_1_output_reg_1),
    .OUTPUT_REG_2(reg_bank_a_1_output_reg_2), .OUTPUT_REG_3(reg_bank_a_1_output_reg_3),
    .OUTPUT_REG_4(reg_bank_a_1_output_reg_4));
  REG_BANK_B reg_bank_b_1 (
    .REG_BANK_B_INPUT(mbrs_1_output_mbr_b), .REG_5_WE(ROM_PCU_data[15]), .REG_5_OE(ROM_PCU_data[16]),
    .REG_6_WE(ROM_PCU_data[17]), .REG_6_OE(ROM_PCU_data[18]), .REG_7_WE(ROM_PCU_data[19]),
    .REG_7_OE(ROM_PCU_data[20]), .REG_8_WE(ROM_PCU_data[21]), .REG_8_OE(ROM_PCU_data[22]),
    .CLOCK(controlled_buffer_17_out), .OUTPUT_REG_5(reg_bank_b_1_output_reg_5),
    .OUTPUT_REG_6(reg_bank_b_1_output_reg_6), .OUTPUT_REG_7(reg_bank_b_1_output_reg_7),
    .OUTPUT_REG_8(reg_bank_b_1_output_reg_8));
  Counter #(.max('h1f), .width(5)) PROGRAM_COUNTER (
    .up(ROM_PCU_data[13]), .count(ROM_PCU_data[14]), .clk(controlled_buffer_17_out), .Q(PROGRAM_COUNTER_q));  // open: clr, load, D, carry
  Counter #(.max('h1f), .width(5)) BLOCK_MOVE_COUNTER_DESTINATION (
    .load(ROM_PCU_data[42]), .up(1'b1), .count(ROM_PCU_data[41]), .clk(controlled_buffer_17_out),
    .D(mars_1_output_mar_b), .Q(BLOCK_MOVE_COUNTER_DESTINATION_q));  // open: clr, carry
  assign controlled_buffer_3_out = nor_1_out ? BLOCK_MOVE_COUNTER_DESTINATION_q : 5'bz;  // Controlled_Buffer controlled_buffer_19
  nor nor_1 (nor_1_out, ROM_PCU_data[50], ROM_PCU_data[49]);
  assign controlled_buffer_4_out = ROM_PCU_data[50] ? block_incrementer_1_to_mar_a : 5'bz;  // Controlled_Buffer controlled_buffer_20
  not not_4 (not_4_out, final_decoder_1_move_to_mem_b);
  assign controlled_buffer_21_out = not_4_out ? mars_1_output_mar_b : 5'bz;  // Controlled_Buffer controlled_buffer_21
  nor nor_2 (nor_2_out, instruction_splitter_1_flag, nand_1_out);
  nand nand_1 (nand_1_out, not_7_out, final_decoder_1_block_move);
  assign controlled_buffer_3_out = ROM_PCU_data[50] ? block_incrementer_1_to_mar_b : 5'bz;  // Controlled_Buffer controlled_buffer_22
  assign controlled_buffer_23_out = BLOCK_LOAD ? mars_1_output_mar_b : 5'bz;  // Controlled_Buffer controlled_buffer_23
  RAM #(.addrWidth(5), .dataWidth(16)) RAM_B (
    .addr(controlled_buffer_23_out), .we(ROM_PCU_data[43]), .oe(ROM_PCU_data[44]),
    .clk(controlled_buffer_17_out), .din(mbrs_1_output_mbr_b), .dout(RAM_B_dout));
  assign controlled_buffer_23_out = nor_2_out ? controlled_buffer_21_out : 5'bz;  // Controlled_Buffer controlled_buffer_24
  assign controlled_buffer_25_out = and_1_out ? INST_RAM_dout : 16'bz;  // Controlled_Buffer controlled_buffer_25
  nor nor_3 (nor_3_out, final_decoder_1_move_to_mem_b, final_decoder_1_move_to_mem_a);
  and and_1 (and_1_out, nor_3_out, not_5_out);
  not not_5 (not_5_out, final_decoder_1_block_move);
  not not_6 (not_6_out, and_1_out);
  nor nor_4 (nor_4_out, xor_2_out, and_1_out, not_8_out);
  not not_7 (not_7_out, final_decoder_1_move_to_mem_a);
  assign bus_terminus_1_to_mbrb = not_2_out ? RAM_B_dout : 16'bz;  // Controlled_Buffer controlled_buffer_26
  assign controlled_buffer_23_out = final_decoder_1_move_to_mem_a ? controlled_buffer_30_out : 5'bz;  // Controlled_Buffer controlled_buffer_27
  not not_8 (not_8_out, ROM_PCU_data[6]);
  assign controlled_buffer_4_out = nor_4_out ? controlled_buffer_39_out : 5'bz;  // Controlled_Buffer controlled_buffer_28
  assign controlled_buffer_25_out = not_6_out ? controlled_buffer_31_out : 16'bz;  // Controlled_Buffer controlled_buffer_29
  assign controlled_buffer_30_out = final_decoder_1_move_to_mem_b ? mars_1_output_mar_a : 5'bz;  // Controlled_Buffer controlled_buffer_30
  or or_1 (or_1_out, final_decoder_1_move_to_mem_b, final_decoder_1_move_to_mem_a);
  MARS mars_1 (
    .TO_MAR_Z(PROGRAM_COUNTER_q), .CLOCK(controlled_buffer_17_out), .MAR_Z_WE(ROM_PCU_data[4]),
    .TO_MAR_A(controlled_buffer_4_out), .MAR_A_WE(ROM_PCU_data[5]), .MAR_B_WE(ROM_PCU_data[6]),
    .TO_MAR_B(controlled_buffer_3_out), .OUTPUT_MAR_Z(mars_1_output_mar_z),
    .OUTPUT_MAR_A(mars_1_output_mar_a), .OUTPUT_MAR_B(mars_1_output_mar_b));
  MBRS mbrs_1 (
    .TO_MBR_Z(controlled_buffer_25_out), .CLOCK(controlled_buffer_17_out), .MBR_Z_WE(ROM_PCU_data[7]),
    .MBR_Z_OE(ROM_PCU_data[8]), .TO_MBR_A(bus_terminus_1_to_mbr_a), .MBR_A_WE(ROM_PCU_data[9]),
    .MBR_A_OE(ROM_PCU_data[10]), .MBR_B_WE(ROM_PCU_data[11]), .MBR_B_OE(ROM_PCU_data[12]),
    .TO_MBR_B(bus_terminus_1_to_mbrb), .OUTPUT_MBR_Z(mbrs_1_output_mbr_z),
    .OUTPUT_MBR_A(mbrs_1_output_mbr_a), .OUTPUT_MBR_B(mbrs_1_output_mbr_b));
  BLOCK_INCREMENTER block_incrementer_1 (
    .ADD_A(controlled_buffer_6_out), .CLOCK(controlled_buffer_17_out), .COUNTER_LOAD_ON(ROM_PCU_data[42]),
    .COUNTER_INC_ON_ENABLE(ROM_PCU_data[41]), .ADD_B(controlled_buffer_5_out),
    .TO_MAR_A(block_incrementer_1_to_mar_a), .TO_MAR_B(block_incrementer_1_to_mar_b));
  assign controlled_buffer_31_out = or_1_out ? controlled_buffer_31_out : 16'bz;  // Controlled_Buffer controlled_buffer_31
  not not_9 (not_9_out, final_decoder_1_move_to_mem_a);
  assign controlled_buffer_32_out = not_9_out ? mars_1_output_mar_a : 5'bz;  // Controlled_Buffer controlled_buffer_32
  assign controlled_buffer_32_out = final_decoder_1_move_to_mem_a ? mars_1_output_mar_b : 5'bz;  // Controlled_Buffer controlled_buffer_33
  not not_10 (not_10_out, final_decoder_1_move_to_mem_a);
  assign controlled_buffer_34_out = nand_2_out ? mars_1_output_mar_a : 5'bz;  // Controlled_Buffer controlled_buffer_34
  assign controlled_buffer_34_out = BLOCK_LOAD ? mars_1_output_mar_a : 5'bz;  // Controlled_Buffer controlled_buffer_35
  RAM #(.addrWidth(5), .dataWidth(16)) RAM_A (
    .addr(controlled_buffer_34_out), .we(ROM_PCU_data[45]), .oe(ROM_PCU_data[46]),
    .clk(controlled_buffer_17_out), .din(mbrs_1_output_mbr_a), .dout(RAM_A_dout));
  assign controlled_buffer_34_out = final_decoder_1_move_to_mem_a ? mars_1_output_mar_a : 5'bz;  // Controlled_Buffer controlled_buffer_36
  RAM #(.addrWidth(5), .dataWidth(16)) INST_RAM (
    .addr(mars_1_output_mar_z), .we(ROM_PCU_data[0]), .oe(ROM_PCU_data[1]), .clk(controlled_buffer_17_out),
    .din(mbrs_1_output_mbr_z), .dout(INST_RAM_dout));
  RAM #(.addrWidth(5), .dataWidth(16)) SYS_RAM (
    .addr(controlled_buffer_32_out), .we(ROM_PCU_data[2]), .oe(ROM_PCU_data[3]),
    .clk(controlled_buffer_17_out), .din(matmult_results_1_output_prod1_topleft),
    .dout(controlled_buffer_31_out));
  Counter #(.max('hf), .width(4)) ROM_CLOCK_COUNTER (
    .load(ROM_PCU_data[47]), .up(1'b1), .count(1'b1), .clk(controlled_buffer_17_out), .D(4'b0000),
    .Q(ROM_CLOCK_COUNTER_q));  // open: clr, carry
  nand nand_2 (nand_2_out, not_10_out, final_decoder_1_block_move, instruction_splitter_1_flag);
  assign bus_terminus_1_to_mbr_a = not_2_out ? RAM_A_dout : 16'bz;  // Controlled_Buffer controlled_buffer_37
  assign controlled_buffer_38_out = final_decoder_1_block_store ? mars_1_output_mar_a : 5'bz;  // Controlled_Buffer controlled_buffer_38
  Counter #(.max('h1f), .width(5)) BLOCK_STORE_COUNTER (
    .load(ROM_PCU_data[42]), .up(1'b1), .count(ROM_PCU_data[41]), .clk(controlled_buffer_17_out),
    .D(controlled_buffer_38_out), .Q(BLOCK_STORE_COUNTER_q));  // open: clr, carry
  assign controlled_buffer_39_out = final_decoder_1_block_store ? BLOCK_STORE_COUNTER_q : 5'bz;  // Controlled_Buffer controlled_buffer_39
  Counter #(.max('h1f), .width(5)) BLOCK_MOVE_COUNTER_SOURCE (
    .load(ROM_PCU_data[42]), .up(1'b1), .count(ROM_PCU_data[41]), .clk(controlled_buffer_17_out),
    .D(mars_1_output_mar_a), .Q(BLOCK_MOVE_COUNTER_SOURCE_q));  // open: clr, carry
  ExactlyOne xor_1 (.out(xor_1_out), .in0(ROM_PCU_data[49]), .in1(ROM_PCU_data[50]), .in2(not_11_out));
  xor xor_2 (xor_2_out, xor_1_out, final_decoder_1_block_move);
  assign controlled_buffer_4_out = xor_2_out ? BLOCK_MOVE_COUNTER_SOURCE_q : 5'bz;  // Controlled_Buffer controlled_buffer_40
  not not_11 (not_11_out, not_6_out);
  ROM #(.dataWidth(56)) ROM_PCU (.addr({OPCODE_REG_q[3:0], ROM_CLOCK_COUNTER_q}), .data(ROM_PCU_data));

  // Notes on the sheet:
  //   contents of ROM_PCU (hex, n*v repeats v):
  //   600002010 6002 2080 800002100 2800400002060 11*0 500000002000 2a00 80b400 181012000 800600002000
  //   11*0 40000002000 2008 20000002080 18000000002160 c0000000002a08 2a0000003480 18000000002160
  //   c0000000002a08 2a0000003480 18000000002160 c0000000002a08 2a0000003480 18000000002160 c0000000002a00
  //   2a0000003400 800600002000 500000002000 2a00 80b400 181012000 800600002000 11*0 800600002004 47*0
  //   5040000002060 500000002000 2a60 2000080b400 4000000002060 500000002000 2a60 20002023400
  //   4000000002060 500000002000 2a60 20008083400 4000000002060 500000002000 2a60 820620203400 42000002004
  //   20000002000 2020 24000002004 2020 28000002004 2020 810600002004 8*0 801655552000 15*0 500000002000
  //   2a00 80b400 181012000 800600002000 11*0 500000002000 2a00 80b400 181012000 800600002000 59*0 2008
  //   2080 18000000002100 c0000000002a00 a80600003400
endmodule

module NOP_HALT (
  input  A,
  input  B,
  input  C,
  input  D,
  input  E,
  output NOP,
  output HALT
);

  wire not_1_out, not_2_out;

  not not_1 (not_1_out, A);
  not not_2 (not_2_out, E);
  and and_1 (NOP, not_1_out, B, C, D, not_2_out);
  and and_2 (HALT, A, B, C, D, not_2_out);
endmodule

module SAAF_SUTRA_NEW_WALA (
  input  INST_RAM_WE,
  input  INST_RAM_OE,
  input  SYS_RAM_WE,
  input  SYS_RAM_OE,
  input  MAR_Z_WE,
  input  MAR_A_WE,
  input  MAR_B_WE,
  input  MBR_Z_WE,
  input  MBR_Z_OE,
  input  MBR_A_WE,
  input  MBR_A_OE,
  input  MBR_B_WE,
  input  MBR_B_OE,
  input  COUNTER_INC_ON,
  input  COUNTER_INC_BY_1,
  input  REG_5_WE,
  input  REG_5_OE,
  input  REG_6_WE,
  input  REG_6_OE,
  input  REG_7_WE,
  input  REG_7_OE,
  input  REG_8_WE,
  input  REG_8_OE,
  input  REG_1_WE,
  input  REG_1_OE,
  input  REG_2_WE,
  input  REG_2_OE,
  input  REG_3_WE,
  input  REG_3_OE,
  input  REG_4_WE,
  input  REG_4_OE,
  input  OVERFLOW_REG_WE,
  input  OUTPUT_REG_WE,
  input  OPCODE_REG_INIT_CB,
  input  OPCODE_REG_WE,
  input  INST_SPLITTER_WE,
  input  MATMULT_ALL_PRODS_WE,
  input  MATMULT_PROD1_OE,
  input  MATMULT_PROD2_OE,
  input  MATMULT_PROD3_OE,
  input  MATMULT_PROD4_OE,
  input  BLOCK_INCREMENTER_ON_ENABLE,
  input  BLOCK_LOAD_ON,
  input  RAM_B_WE,
  input  RAM_B_OE,
  input  RAM_A_WE,
  input  RAM_A_OE,
  input  ROM_CLK_COUNT_RESET,
  input  BLOCK_INCREMENTER_ADD_ALLOW,
  input  MARS_ALLOW,
  input  BLOCK_INCREMENTER_INC_ADD_ALLOW,
  input  TERMINAL_A_WE,
  input  TERMINAL_B_WE,
  input  B1,
  input  B2,
  input  TERMINUS_OE,
  output NOP,
  output BLOCK_LOAD,
  output NOT_DONE,
  output RESERVED
);

  wire CLK_out, controlled_buffer_17_out, final_decoder_1_block_store, final_decoder_1_mat_mult,
       final_decoder_1_move_to_mem_a, final_decoder_1_move_to_mem_b, final_decoder_1_store,
       final_decoder_1_store_overflow, instruction_splitter_1_flag, nop_halt_1_halt, nor_1_out, not_1_out,
       not_2_out, not_3_out, not_4_out, not_5_out, not_6_out, not_7_out, not_8_out, not_9_out, or_1_out;
  wire [3:0] ROM_CLOCK_COUNTER_q;
  wire [4:0] block_incrementer_1_to_mar_a, block_incrementer_1_to_mar_b, BLOCK_STORE_COUNTER_q,
       controlled_buffer_1_out, controlled_buffer_3_out, controlled_buffer_4_out, controlled_buffer_5_out,
       controlled_buffer_6_out, controlled_buffer_20_out, controlled_buffer_22_out, controlled_buffer_28_out,
       controlled_buffer_30_out, controlled_buffer_32_out, controlled_buffer_35_out,
       controlled_buffer_36_out, instruction_splitter_1_add_a, instruction_splitter_1_add_b,
       instruction_splitter_1_opcode, mars_1_output_mar_a, mars_1_output_mar_b, mars_1_output_mar_z,
       OPCODE_REG_q, PROGRAM_COUNTER_q;
  wire [15:0] alu_1_overflow_out, alu_1_result, bus_terminus_1_to_mbr_a, bus_terminus_1_to_mbr_z_from_term_a,
       bus_terminus_1_to_mbrb, controlled_buffer_8_out, controlled_buffer_9_out, controlled_buffer_10_out,
       controlled_buffer_11_out, controlled_buffer_13_out, controlled_buffer_14_out,
       controlled_buffer_15_out, controlled_buffer_16_out, controlled_buffer_23_out,
       controlled_buffer_29_out, INST_RAM_dout, mat_mult_1_prod1_topleft, mat_mult_1_prod2_topright,
       mat_mult_1_prod3_bottomleft, mat_mult_1_prod4_bottomright, matmult_results_1_output_prod1_topleft,
       mbrs_1_output_mbr_a, mbrs_1_output_mbr_b, mbrs_1_output_mbr_z, OUTPUT_REG_q, OVERFLOW_REG_q,
       RAM_A_dout, RAM_B_dout, reg_bank_a_1_output_reg_1, reg_bank_a_1_output_reg_2,
       reg_bank_a_1_output_reg_3, reg_bank_a_1_output_reg_4, reg_bank_b_1_output_reg_5,
       reg_bank_b_1_output_reg_6, reg_bank_b_1_output_reg_7, reg_bank_b_1_output_reg_8, SYS_RAM_dout;
  wire [55:0] ROM_PCU_data;

  not not_1 (not_1_out, ROM_PCU_data[33]);
  FINAL_DECODER final_decoder_1 (
    .A(instruction_splitter_1_flag), .B(instruction_splitter_1_opcode[3]),
    .C(instruction_splitter_1_opcode[2]), .D(instruction_splitter_1_opcode[1]),
    .E(instruction_splitter_1_opcode[0]), .RESERVED(RESERVED), .BLOCK_MOVE(NOT_DONE),
    .BLOCK_LOAD(BLOCK_LOAD), .BLOCK_STORE(final_decoder_1_block_store),
    .MOVE_TO_MEM_A(final_decoder_1_move_to_mem_a), .MOVE_TO_MEM_B(final_decoder_1_move_to_mem_b),
    .STORE(final_decoder_1_store), .STORE_OVERFLOW(final_decoder_1_store_overflow),
    .MAT_MULT(final_decoder_1_mat_mult));  // open: MEM_SWAP, REG_SWAP
  not not_2 (not_2_out, ROM_PCU_data[55]);
  assign controlled_buffer_1_out = not_1_out ? instruction_splitter_1_opcode : 5'bz;  // Controlled_Buffer controlled_buffer_1
  MATMULT_RESULTS matmult_results_1 (
    .CLOCK(controlled_buffer_17_out), .PROD1_TOPLEFT(mat_mult_1_prod1_topleft),
    .PROD1_TOPLEFT_WE(ROM_PCU_data[36]), .PROD1_TOPLEFT_OE(ROM_PCU_data[37]),
    .PROD2_TOPRIGHT(mat_mult_1_prod2_topright), .PROD2_TOPRIGHT_WE(ROM_PCU_data[36]),
    .PROD2_TOPRIGHT_OE(ROM_PCU_data[38]), .PROD3_BOTTOMLEFT(mat_mult_1_prod3_bottomleft),
    .PROD3_BOTTOMLEFT_WE(ROM_PCU_data[36]), .PROD3_BOTTOMLEFT_OE(ROM_PCU_data[39]),
    .PROD4_BOTTOMRIGHT(mat_mult_1_prod4_bottomright), .PROD4_BOTTOMRIGHT_WE(ROM_PCU_data[36]),
    .PROD4_BOTTOMRIGHT_OE(ROM_PCU_data[40]), .OUTPUT_PROD1_TOPLEFT(matmult_results_1_output_prod1_topleft),
    .OUTPUT_PROD2_TOPRIGHT(matmult_results_1_output_prod1_topleft),
    .OUTPUT_PROD3_BOTTOMLEFT(matmult_results_1_output_prod1_topleft),
    .OUTPUT_PROD4_BOTTOMRIGHT(matmult_results_1_output_prod1_topleft));
  Register #(.width(5)) OPCODE_REG (
    .D(controlled_buffer_1_out), .en(ROM_PCU_data[34]), .clk(controlled_buffer_17_out), .Q(OPCODE_REG_q));  // open: clr
  assign controlled_buffer_1_out = ROM_PCU_data[33] ? {5{1'b0}} : 5'bz;  // Controlled_Buffer controlled_buffer_2
  assign controlled_buffer_3_out = ROM_PCU_data[49] ? instruction_splitter_1_add_b : 5'bz;  // Controlled_Buffer controlled_buffer_3
  BUS_TERMINUS bus_terminus_1 (
    .DATA_A(mbrs_1_output_mbr_z), .TERMINAL_A_WE(ROM_PCU_data[51]), .CLOCK(controlled_buffer_17_out),
    .DATA_B(mbrs_1_output_mbr_z), .TERMINAL_B_WE(ROM_PCU_data[52]), .B_1(ROM_PCU_data[53]),
    .B_2(ROM_PCU_data[54]), .OE(ROM_PCU_data[55]), .TO_MBR_A(bus_terminus_1_to_mbr_a),
    .TO_MBR_Z_FROM_TERM_A(bus_terminus_1_to_mbr_z_from_term_a), .TO_MBRB(bus_terminus_1_to_mbrb),
    .TO_MBR_Z_FROM_TERM_B(bus_terminus_1_to_mbr_z_from_term_a));
  assign controlled_buffer_4_out = ROM_PCU_data[49] ? instruction_splitter_1_add_a : 5'bz;  // Controlled_Buffer controlled_buffer_4
  assign controlled_buffer_5_out = ROM_PCU_data[48] ? instruction_splitter_1_add_b : 5'bz;  // Controlled_Buffer controlled_buffer_5
  Instruction_splitter instruction_splitter_1 (
    .Instruction(mbrs_1_output_mbr_z), .Write_Enable(ROM_PCU_data[35]), .Clock(controlled_buffer_17_out),
    .Add_B(instruction_splitter_1_add_b), .Add_A(instruction_splitter_1_add_a),
    .Opcode(instruction_splitter_1_opcode), .Flag(instruction_splitter_1_flag));
  assign controlled_buffer_6_out = ROM_PCU_data[48] ? instruction_splitter_1_add_a : 5'bz;  // Controlled_Buffer controlled_buffer_6
  MAT_MULT mat_mult_1 (
    .REG_1(controlled_buffer_16_out), .REG_5(controlled_buffer_15_out), .REG_2(controlled_buffer_14_out),
    .REG_7(controlled_buffer_13_out), .REG_6(controlled_buffer_11_out), .REG_8(controlled_buffer_10_out),
    .REG_3(controlled_buffer_9_out), .REG_4(controlled_buffer_8_out),
    .PROD1_TOPLEFT(mat_mult_1_prod1_topleft), .PROD2_TOPRIGHT(mat_mult_1_prod2_topright),
    .PROD3_BOTTOMLEFT(mat_mult_1_prod3_bottomleft), .PROD4_BOTTOMRIGHT(mat_mult_1_prod4_bottomright));
  Register #(.width(16)) OVERFLOW_REG (
    .D(alu_1_overflow_out), .en(ROM_PCU_data[31]), .clk(controlled_buffer_17_out), .Q(OVERFLOW_REG_q));  // open: clr
  Register #(.width(16)) OUTPUT_REG (
    .D(alu_1_result), .en(ROM_PCU_data[32]), .clk(controlled_buffer_17_out), .Q(OUTPUT_REG_q));  // open: clr
  assign matmult_results_1_output_prod1_topleft = final_decoder_1_store_overflow ? OVERFLOW_REG_q : 16'bz;  // Controlled_Buffer controlled_buffer_7
  assign controlled_buffer_8_out = final_decoder_1_mat_mult ? reg_bank_a_1_output_reg_4 : 16'bz;  // Controlled_Buffer controlled_buffer_8
  assign controlled_buffer_9_out = final_decoder_1_mat_mult ? reg_bank_a_1_output_reg_3 : 16'bz;  // Controlled_Buffer controlled_buffer_9
  assign controlled_buffer_10_out = final_decoder_1_mat_mult ? reg_bank_b_1_output_reg_8 : 16'bz;  // Controlled_Buffer controlled_buffer_10
  assign controlled_buffer_11_out = final_decoder_1_mat_mult ? reg_bank_b_1_output_reg_6 : 16'bz;  // Controlled_Buffer controlled_buffer_11
  assign matmult_results_1_output_prod1_topleft = final_decoder_1_store ? OUTPUT_REG_q : 16'bz;  // Controlled_Buffer controlled_buffer_12
  NOP_HALT nop_halt_1 (
    .A(instruction_splitter_1_flag), .B(instruction_splitter_1_opcode[3]),
    .C(instruction_splitter_1_opcode[2]), .D(instruction_splitter_1_opcode[1]),
    .E(instruction_splitter_1_opcode[0]), .NOP(NOP), .HALT(nop_halt_1_halt));
  ALU alu_1 (
    .A(reg_bank_a_1_output_reg_1), .B(reg_bank_b_1_output_reg_5), .Flag(instruction_splitter_1_flag),
    .Opcode(instruction_splitter_1_opcode), .RESULT(alu_1_result), .OVERFLOW_OUT(alu_1_overflow_out));
  assign controlled_buffer_13_out = final_decoder_1_mat_mult ? reg_bank_b_1_output_reg_7 : 16'bz;  // Controlled_Buffer controlled_buffer_13
  assign controlled_buffer_14_out = final_decoder_1_mat_mult ? reg_bank_a_1_output_reg_2 : 16'bz;  // Controlled_Buffer controlled_buffer_14
  assign controlled_buffer_15_out = final_decoder_1_mat_mult ? reg_bank_b_1_output_reg_5 : 16'bz;  // Controlled_Buffer controlled_buffer_15
  assign controlled_buffer_16_out = final_decoder_1_mat_mult ? reg_bank_a_1_output_reg_1 : 16'bz;  // Controlled_Buffer controlled_buffer_16
  assign controlled_buffer_17_out = not_3_out ? CLK_out : 1'bz;  // Controlled_Buffer controlled_buffer_17
  Clock CLK (.out(CLK_out));
  assign controlled_buffer_17_out = not_3_out ? CLK_out : 1'bz;  // Controlled_Buffer controlled_buffer_18
  not not_3 (not_3_out, nop_halt_1_halt);
  REG_BANK_A reg_bank_a_1 (
    .REG_BANK_A_INPUT(mbrs_1_output_mbr_a), .REG_1_WE(ROM_PCU_data[23]), .REG_1_OE(ROM_PCU_data[24]),
    .REG_2_WE(ROM_PCU_data[25]), .REG_2_OE(ROM_PCU_data[26]), .REG_3_WE(ROM_PCU_data[27]),
    .REG_3_OE(ROM_PCU_data[28]), .REG_4_WE(ROM_PCU_data[29]), .REG_4_OE(ROM_PCU_data[30]),
    .CLOCK(controlled_buffer_17_out), .OUTPUT_REG_1(reg_bank_a_1_output_reg_1),
    .OUTPUT_REG_2(reg_bank_a_1_output_reg_2), .OUTPUT_REG_3(reg_bank_a_1_output_reg_3),
    .OUTPUT_REG_4(reg_bank_a_1_output_reg_4));
  REG_BANK_B reg_bank_b_1 (
    .REG_BANK_B_INPUT(mbrs_1_output_mbr_b), .REG_5_WE(ROM_PCU_data[15]), .REG_5_OE(ROM_PCU_data[16]),
    .REG_6_WE(ROM_PCU_data[17]), .REG_6_OE(ROM_PCU_data[18]), .REG_7_WE(ROM_PCU_data[19]),
    .REG_7_OE(ROM_PCU_data[20]), .REG_8_WE(ROM_PCU_data[21]), .REG_8_OE(ROM_PCU_data[22]),
    .CLOCK(controlled_buffer_17_out), .OUTPUT_REG_5(reg_bank_b_1_output_reg_5),
    .OUTPUT_REG_6(reg_bank_b_1_output_reg_6), .OUTPUT_REG_7(reg_bank_b_1_output_reg_7),
    .OUTPUT_REG_8(reg_bank_b_1_output_reg_8));
  Counter #(.max('h1f), .width(5)) PROGRAM_COUNTER (
    .up(ROM_PCU_data[13]), .count(ROM_PCU_data[14]), .clk(controlled_buffer_17_out), .Q(PROGRAM_COUNTER_q));  // open: clr, load, D, carry
  assign controlled_buffer_4_out = ROM_PCU_data[50] ? block_incrementer_1_to_mar_a : 5'bz;  // Controlled_Buffer controlled_buffer_19
  not not_4 (not_4_out, final_decoder_1_move_to_mem_b);
  assign controlled_buffer_20_out = not_4_out ? mars_1_output_mar_b : 5'bz;  // Controlled_Buffer controlled_buffer_20
  assign controlled_buffer_3_out = ROM_PCU_data[50] ? block_incrementer_1_to_mar_b : 5'bz;  // Controlled_Buffer controlled_buffer_21
  RAM #(.addrWidth(5), .dataWidth(16)) RAM_B (
    .addr(controlled_buffer_22_out), .we(ROM_PCU_data[43]), .oe(ROM_PCU_data[44]),
    .clk(controlled_buffer_17_out), .din(mbrs_1_output_mbr_b), .dout(RAM_B_dout));
  assign controlled_buffer_22_out = not_5_out ? controlled_buffer_20_out : 5'bz;  // Controlled_Buffer controlled_buffer_22
  assign controlled_buffer_23_out = nor_1_out ? INST_RAM_dout : 16'bz;  // Controlled_Buffer controlled_buffer_23
  nor nor_1 (nor_1_out, final_decoder_1_move_to_mem_b, final_decoder_1_move_to_mem_a);
  not not_5 (not_5_out, final_decoder_1_move_to_mem_a);
  assign bus_terminus_1_to_mbrb = not_2_out ? RAM_B_dout : 16'bz;  // Controlled_Buffer controlled_buffer_24
  assign controlled_buffer_22_out = not_5_out ? controlled_buffer_28_out : 5'bz;  // Controlled_Buffer controlled_buffer_25
  not not_6 (not_6_out, ROM_PCU_data[6]);
  not not_7 (not_7_out, nor_1_out);
  assign controlled_buffer_4_out = not_6_out ? controlled_buffer_36_out : 5'bz;  // Controlled_Buffer controlled_buffer_26
  assign controlled_buffer_23_out = not_7_out ? controlled_buffer_29_out : 16'bz;  // Controlled_Buffer controlled_buffer_27
  assign controlled_buffer_28_out = final_decoder_1_move_to_mem_b ? mars_1_output_mar_a : 5'bz;  // Controlled_Buffer controlled_buffer_28
  or or_1 (or_1_out, final_decoder_1_move_to_mem_b, final_decoder_1_move_to_mem_a);
  MARS mars_1 (
    .TO_MAR_Z(PROGRAM_COUNTER_q), .CLOCK(controlled_buffer_17_out), .MAR_Z_WE(ROM_PCU_data[4]),
    .TO_MAR_A(controlled_buffer_4_out), .MAR_A_WE(ROM_PCU_data[5]), .MAR_B_WE(ROM_PCU_data[6]),
    .TO_MAR_B(controlled_buffer_3_out), .OUTPUT_MAR_Z(mars_1_output_mar_z),
    .OUTPUT_MAR_A(mars_1_output_mar_a), .OUTPUT_MAR_B(mars_1_output_mar_b));
  MBRS mbrs_1 (
    .TO_MBR_Z(controlled_buffer_23_out), .CLOCK(controlled_buffer_17_out), .MBR_Z_WE(ROM_PCU_data[7]),
    .MBR_Z_OE(ROM_PCU_data[8]), .TO_MBR_A(bus_terminus_1_to_mbr_a), .MBR_A_WE(ROM_PCU_data[9]),
    .MBR_A_OE(ROM_PCU_data[10]), .MBR_B_WE(ROM_PCU_data[11]), .MBR_B_OE(ROM_PCU_data[12]),
    .TO_MBR_B(bus_terminus_1_to_mbrb), .OUTPUT_MBR_Z(mbrs_1_output_mbr_z),
    .OUTPUT_MBR_A(mbrs_1_output_mbr_a), .OUTPUT_MBR_B(mbrs_1_output_mbr_b));
  BLOCK_INCREMENTER block_incrementer_1 (
    .ADD_A(controlled_buffer_6_out), .CLOCK(controlled_buffer_17_out), .COUNTER_LOAD_ON(ROM_PCU_data[42]),
    .COUNTER_INC_ON_ENABLE(ROM_PCU_data[41]), .ADD_B(controlled_buffer_5_out),
    .TO_MAR_A(block_incrementer_1_to_mar_a), .TO_MAR_B(block_incrementer_1_to_mar_b));
  assign controlled_buffer_29_out = or_1_out ? SYS_RAM_dout : 16'bz;  // Controlled_Buffer controlled_buffer_29
  not not_8 (not_8_out, final_decoder_1_move_to_mem_a);
  assign controlled_buffer_30_out = not_8_out ? mars_1_output_mar_a : 5'bz;  // Controlled_Buffer controlled_buffer_30
  assign controlled_buffer_30_out = final_decoder_1_move_to_mem_a ? mars_1_output_mar_b : 5'bz;  // Controlled_Buffer controlled_buffer_31
  not not_9 (not_9_out, final_decoder_1_move_to_mem_a);
  assign controlled_buffer_32_out = not_9_out ? mars_1_output_mar_a : 5'bz;  // Controlled_Buffer controlled_buffer_32
  RAM #(.addrWidth(5), .dataWidth(16)) RAM_A (
    .addr(controlled_buffer_32_out), .we(ROM_PCU_data[45]), .oe(ROM_PCU_data[46]),
    .clk(controlled_buffer_17_out), .din(mbrs_1_output_mbr_a), .dout(RAM_A_dout));
  assign controlled_buffer_32_out = final_decoder_1_move_to_mem_a ? mars_1_output_mar_a : 5'bz;  // Controlled_Buffer controlled_buffer_33
  RAM #(.addrWidth(5), .dataWidth(16)) INST_RAM (
    .addr(mars_1_output_mar_z), .we(ROM_PCU_data[0]), .oe(ROM_PCU_data[1]), .clk(controlled_buffer_17_out),
    .din(mbrs_1_output_mbr_z), .dout(INST_RAM_dout));
  RAM #(.addrWidth(5), .dataWidth(16)) SYS_RAM (
    .addr(controlled_buffer_30_out), .we(ROM_PCU_data[2]), .oe(ROM_PCU_data[3]),
    .clk(controlled_buffer_17_out), .din(matmult_results_1_output_prod1_topleft), .dout(SYS_RAM_dout));
  Counter #(.max('hf), .width(4)) ROM_CLOCK_COUNTER (
    .load(ROM_PCU_data[47]), .up(1'b1), .count(1'b1), .clk(controlled_buffer_17_out), .D(4'b0000),
    .Q(ROM_CLOCK_COUNTER_q));  // open: clr, carry
  assign bus_terminus_1_to_mbr_a = not_2_out ? RAM_A_dout : 16'bz;  // Controlled_Buffer controlled_buffer_34
  assign controlled_buffer_35_out = final_decoder_1_block_store ? mars_1_output_mar_a : 5'bz;  // Controlled_Buffer controlled_buffer_35
  Counter #(.max('h1f), .width(5)) BLOCK_STORE_COUNTER (
    .load(ROM_PCU_data[42]), .up(1'b1), .count(ROM_PCU_data[41]), .clk(controlled_buffer_17_out),
    .D(controlled_buffer_35_out), .Q(BLOCK_STORE_COUNTER_q));  // open: clr, carry
  assign controlled_buffer_36_out = final_decoder_1_block_store ? BLOCK_STORE_COUNTER_q : 5'bz;  // Controlled_Buffer controlled_buffer_36
  ROM #(.dataWidth(56)) ROM_PCU (.addr({OPCODE_REG_q[3:0], ROM_CLOCK_COUNTER_q}), .data(ROM_PCU_data));

  // Notes on the sheet:
  //   contents of ROM_PCU (hex, n*v repeats v):
  //   600002010 6002 2080 800002100 2800400002060 11*0 500000002000 2a00 80b400 181012000 800600002000
  //   27*0 500000002000 2a00 80b400 181012000 800600002000 11*0 800600002004 47*0 5040000002060
  //   500000002000 2a60 2000080b400 4000000002060 500000002000 2a60 20002023400 4000000002060 500000002000
  //   2a60 20008083400 4000000002060 500000002000 2a60 820620203400 42000002004 20000002000 2020
  //   24000002004 2020 28000002004 2020 810600002004 8*0 801655552000 15*0 500000002000 2a00 80b400
  //   181012000 800600002000 11*0 500000002000 2a00 80b400 181012000 800600002000 59*0 2008 2080
  //   18000000002100 c0000000002a00 a80600003400
endmodule
